# Fritzing sketch Aquaduino (saved by Fritzing 0.9.2b)

parts:
  Part2 = LCD Keypad Shield
  7805_Regulator = Voltage Regulator - 5V [package="TO220 [THT]"]
  Relay_1 = Module 4 Relais 5V [package="Module 4 Relais 5V"]
  D1 = Rectifier Diode [part_number=1N4001 package="300 mil [THT]"]
  Servo_Fish_Feeder = Basic Servo
  DS1307_RTC_module = Adafruit DS1307 RTC Breakout [part_number="Adafruit #264"]
  JACK1 = 2.1mm DC Barrel Jack

nets:
  N1: Part2.A4(SDA), DS1307_RTC_module.SDA
  N2: Part2.A5(CLK), DS1307_RTC_module.SCL
  N3: Part2.D11_MOSI, Servo_Fish_Feeder.pulse
  N4: Part2.D12_MISO, Relay_1.IN2
  N5: Part2.D13_SCK, Relay_1.IN1
  N6: Part2.D2, Relay_1.IN4
  N7: Part2.D3, Relay_1.IN3
  GND: Part2.GND, 7805_Regulator.GND, Relay_1.GND, Servo_Fish_Feeder.gnd, DS1307_RTC_module.GND, JACK1.sleeve
  N8: Part2.VIN, 7805_Regulator.input_voltage, D1.cathode
  VCC: 7805_Regulator.output_voltage, Relay_1.VCC, Servo_Fish_Feeder.vcc, DS1307_RTC_module.VCC
  N9: D1.anode, JACK1.center

notes:
  Wire color :
  black = gnd
  blue/cyan/orange = data
  red = +5v
  yellow = +12v
  Relay :
  K1 = aquarium Water Pump Out
  K2 = aquarium Water Pump In
  K3 = aquarium Filter Pump
  K1 = aquarium Led/Light

custom parts:
  LCD Keypad Shield: It consists of a 1602 white character blue backlight LCD. The keypad consists of 5 keys — select, up, right, down and left. To save the digital IO pins, the keypad interface uses only one ADC channel. The key value is read through a 5 stage voltage divider.
  Module 4 Relais 5V: Module 4 Relais 5V 4x SPD-06VDC-SD-C
  Adafruit DS1307 RTC Breakout: This is a great battery-backed real time clock (RTC) that allows your microcontroller project to keep track of time even if it is reprogrammed, or if the power is lost. Perfect for datalogging, clock-building, time stamping, timers and alarms, etc. The DS1307 is the most popular RTC - but it requires 5V power to work (although we've used it with 5V power and 3.3V logic successfully) PCB &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
  2.1mm DC Barrel Jack: 2.1mm DC Barrel Jack with Thru-Hole Connectors (breadboardable)
