# Fritzing sketch CNY70 light proximity sensor_1 (saved by Fritzing 0.8.7b)
breadboards: 1

parts:
  CNY1 = CNY70
  Componente1 = Arduino Uno (Rev3)
  R1 = Resistor [tolerance=±5% resistance=33k package=THT]  # not connected
  R2 = Resistor [tolerance=±5% resistance=330 package=THT]
  R3 = Resistor [tolerance=±5% resistance=330 package=THT]
  LED1 = LED - 5mm [color="Red (633nm)" package="5 mm [THT]"]

nets:
  N1: CNY1.Emisor, CNY1.Catodo, Componente1.5V
  N2: CNY1.Colector, Componente1.A0
  N3: CNY1.Anodo, R2.Pin_1
  N4: Componente1.GND, R2.Pin_0, LED1.cathode
  N5: Componente1.D1/TX, R3.Pin_1
  N6: R3.Pin_0, LED1.anode

notes:
  /*
  * Arduino CNY70 light proximity sensor
  * Developed by Cesário Garcia Mil-Homens
  * http://www.hypatia.pt - Formação e consultoria, Lda.
  *
  */
  int input = A0;
  int output = 1;
  int val = 0;
  void setup() {
  Serial.begin(9600);
  pinMode(input, INPUT);
  pinMode(output, OUTPUT);
  }
  void loop() {
  val = analogRead(input);
  Serial.println(val);
  // delay(500);
  if (val > 25) {
  digitalWrite(output, LOW);
  }
  else {
  digitalWrite(output, HIGH);
  }
  }

custom parts:
  CNY70: Sensor de Infrarojos de corto alcance.
