# Fritzing sketch Digital Clock with Push Buttons (saved by Fritzing 0.9.4)
breadboards: 1

parts:
  S1 = Pushbutton [package="[THT]"]
  S2 = Pushbutton [package="[THT]"]
  Part1 = Arduino Pro Mini v13
  TM1637_4_digit_7_segment = Grove 4 Digit Display
  DS3231 = ZS-042 RTC Module
  R1 = Resistor [tolerance=±5% resistance=10k package=THT]
  R2 = Resistor [tolerance=±5% resistance=10k package=THT]

nets:
  VCC: S1.Pin_1, S1.Pin_2, S2.Pin_1, S2.Pin_2, Part1.VCC, TM1637_4_digit_7_segment.VCC, DS3231.VCC
  N1: S1.Pin_3, S1.Pin_4, Part1.D4, R1.Pin_1
  N2: S2.Pin_3, S2.Pin_4, Part1.D5_PWM, R2.Pin_1
  GND: Part1.GND, Part1.RAW, TM1637_4_digit_7_segment.GND, DS3231.GND, R1.Pin_0, R2.Pin_0
  N3: Part1.A4, DS3231.SDA
  N4: Part1.D3_PWM, TM1637_4_digit_7_segment.DIO
  N5: Part1.D2, TM1637_4_digit_7_segment.CLK

// code stored in the sketch: digital_Clock_with_TM1637_and_DS3231.ino
// We include the libraries used by the program. 
// digital_Clock_with_TM1637_and_DS3231
#include <DS3231.h> 
#include <Wire.h> 
#include <TM1637Display.h> 
// ---------------------------------------------- --------------------------------------- 
// Clock setup 
DS3231 Clock ;

// Setup Display 
#define CLK 2 
#define DIO 3 
TM1637Display display(CLK, DIO);

// We declare the variables and constants 
int Hours, Minutes, Seconds; 
bool H, HH; 
int B_Hours = HIGH; 
int B_Minutes = HIGH; 
// ------------------------------------------------ -------------------------------------

void setup() { 
  Serial.begin(9600);  // We set the serial communication baud rate and initialize it. 
  Wire.begin();  // We initiate I2C communication. 
  display.setBrightness(0x0f);  // We set the brightness of the segment display. 
  pinMode(4, INPUT);  // Pin 4 becomes an input. 
  pinMode(5, INPUT); // Pin 5 becomes an input. 
} 
// ----------------------------------------------- -------------------------------------- 
void  loop ( )  { 
  // The hour values, minutes and seconds are stHoursd on the corresponding variables. 
  Clock.setClockMode(true);
  Hours = Clock.getHour(H, HH); 
  Minutes = Clock.getMinute(); 
  Seconds = Clock.getSecond(); 
  // Serial print on the terminal. 
  Serial.print(Hours); 
  Serial.print(":"); 
  Serial.print(Minutes); 
  Serial.print(":"); 
  Serial.print(Seconds); 
  Serial.println(""); 
  // Local time variable, the sum of hours and minutes, for printing on the display. 
  int Time = ((Hours*100) + Minutes); 
  // Writes the time value with the two dividing points on the display. 
  display.showNumberDecEx(Time, (0x80 >> 1), true,4,0); 
// ------------------------------------------------ ------------------------------------- 
  // First cycle phase for the control of the buttons and the flashing of the colon. 
  for(int i=0; i<50; i++){ 
  B_Hours = digitalRead(5); 
  B_Minutes = digitalRead(4); 
  if(B_Hours == HIGH || B_Minutes == HIGH){ 
    delay(2); 
    }
  else{ 
    delay(2);
    }
    } 
  // We change the values ??of minutes or hours 
  B_Hours = digitalRead(5); 
  B_Minutes = digitalRead(4); 
  if(B_Hours == HIGH && B_Minutes == LOW){ 
    if(Hours<24){Hours=Hours+1; Clock.setHour(Hours);} 
    if(Hours>=24){Clock.setHour(00);} 
    }
  if(B_Minutes == HIGH && B_Hours == LOW){
    if(Minutes<60){Minutes=Minutes+1; Clock.setMinute(Minutes);}
    if(Minutes>=60){Clock.setMinute(00);}
    Clock.setSecond(00);
    }

  //Writes the time value on the display without the two dividing points.
  display.showNumberDecEx(Time, (0x80 >> 2), true,4,0);
//-------------------------------------------------------------------------------------
  //Second cycle phase for the control of the buttons and the flashing of the colon.
  for(int i=0; i<50; i++){
  B_Hours = digitalRead(5);
  B_Minutes = digitalRead(4);
  if(B_Hours == HIGH || B_Minutes == HIGH){
   delay(2);
   }
  else{
    delay(2);
    }
    }
}
