# Fritzing sketch FOKMWPJI101AJZN (saved by Fritzing 0.9.2b)
breadboards: 1

parts:
  Part1 = Arduino Board Ethernet
  R1 = Basic Flex Resistor
  R5 = Resistor [tolerance=±5% resistance=22k package=THT]

nets:
  N1: Part1.A0, R1.pin_1, R5.Pin_1
  N2: Part1.5V, R1.Pin_2
  N3: Part1.GND, R5.Pin_0
