# Fritzing sketch Ligacao_Trava_Relay_KeyPad_oled (saved by Fritzing 0.9.4)
breadboards: 1

parts:
  PowerPlug_1_-_12V = Power plug
  Relay_12V_-_1_Canal = Keyes Relay [package=THT]
  Trava_Solenoide_12v = Solenoid
  Componente1 = Arduino Uno (Rev3)
  Matrix_keypad_4L_x_3c = KEYPAD 4x4
  Grove1 = Grove OLED 128x96
  J1 = Piezo Speaker

nets:
  N1: PowerPlug_1_-_12V.GND, Trava_Solenoide_12v.pin1
  N2: PowerPlug_1_-_12V.VCC, Relay_12V_-_1_Canal.C
  N3: Relay_12V_-_1_Canal.signal, Componente1.D2
  N4: Relay_12V_-_1_Canal.NC, Trava_Solenoide_12v.pin2
  N5: Componente1.D8, Matrix_keypad_4L_x_3c.row2
  N6: Componente1.D9_PWM, Matrix_keypad_4L_x_3c.row3
  N7: Componente1.D13/SCK, J1.pin2
  N8: Componente1.A4/SDA, Grove1.SDA
  N9: Componente1.A5/SCL, Grove1.SCL
  N10: Componente1.D3_PWM, Matrix_keypad_4L_x_3c.col1
  N11: Componente1.D4, Matrix_keypad_4L_x_3c.col2
  N12: Componente1.D5_PWM, Matrix_keypad_4L_x_3c.col3
  N13: Componente1.D6_PWM, Matrix_keypad_4L_x_3c.col4
  N14: Componente1.D7, Matrix_keypad_4L_x_3c.row1
  5V: Componente1.5V, Grove1.VCC
  GND: Componente1.GND, Grove1.GND, J1.pin1

custom parts:
  Keyes Relay: The Keyes 5V relay module is suitable for SCM development, home appliance control. It uses a 5V~12V TIL control signal which can control DC / AC signal.
  KEYPAD 4x4: Matrix keypad 16 buttons, 4 rows x 4 columns

// code stored in the sketch: Ligacao_Trava_Relay.ino
// INCLUINDO BIBLIOTECAS
#include <Arduino.h>
#include <Wire.h>
#include <MicroLCD.h>
#include <Keypad.h> //INCLUSÃO DE BIBLIOTECA

LCD_SSD1306 lcd;
 
const byte qtdLinhas = 4; //QUANTIDADE DE LINHAS DO TECLADO
const byte qtdColunas = 3; //QUANTIDADE DE COLUNAS DO TECLADO
 
//CONSTRUÇÃO DA MATRIZ DE CARACTERES
char matriz_teclas[qtdLinhas][qtdColunas] = {
  {'1','2','3'},
  {'4','5','6'},
  {'7','8','9'},
  {'*','0','#'}
};
 
 
byte PinosqtdLinhas[qtdLinhas] = {3, 4, 5, 6}; //PINOS UTILIZADOS PELAS LINHAS
byte PinosqtdColunas[qtdColunas] = {7, 8, 9}; //PINOS UTILIZADOS PELAS COLUNAS

char* senha = "2020";  //SENHA
int buzzer = 13;
int tempoBuzz = 50;
int position = 0;
int postelamed = 1;
int ledPin = 2;

//INICIALIZAÇÃO DO TECLADO
Keypad meuteclado = Keypad( makeKeymap(matriz_teclas), PinosqtdLinhas, PinosqtdColunas, qtdLinhas, qtdColunas);
 
void setup(){
  Serial.begin(9600); //INICIALIZA A SERIAL
  Serial.println("Aperte uma tecla..."); //IMPRIME O TEXTO NO MONITOR SERIAL
  Serial.println(); //QUEBRA UMA LINHA NO MONITOR SERIAL
  pinMode(buzzer,OUTPUT); 
 pinMode(ledPin, OUTPUT);
digitalWrite(ledPin, HIGH);
 

   inicio_lcd();
//  lcd.begin();
//  lcd.clear();
//  lcd.setCursor(50, 2);
//  lcd.setFontSize(FONT_SIZE_MEDIUM);
//  lcd.println("OLA!");
//  lcd.setCursor(1, 5);
//  lcd.setFontSize(FONT_SIZE_SMALL);
//  lcd.println("Pressione uma tecla:");    
}
  
void loop(){
  char tecla_pressionada = meuteclado.getKey(); //VERIFICA SE ALGUMA DAS TECLAS FOI PRESSIONADA

  if(tecla_pressionada !=0){
        digitalWrite(buzzer, HIGH);
  delay(tempoBuzz);
  digitalWrite(buzzer, LOW); // acionamento do buzzer ao apertar qualquer tecla

  if (tecla_pressionada == senha[position]) // verifica se o dígito apertado corresponde ao equivalente da senha
{

  if (position == 0){
    lcd.clear();
  }
    position ++;
    postelamed = postelamed + 10;
    lcd.setFontSize(FONT_SIZE_MEDIUM);
    lcd.setCursor(postelamed,1); 
    lcd.print("*");

}
else { // retorna a leitura para a primeira posição de leitura da senha quando o dígito apertado não corresponde ao correto 
    position = 0;
    lcd.clear();
    lcd.setCursor(1, 1);
    lcd.setFontSize(FONT_SIZE_MEDIUM); 
    lcd.print("SENHA INVALIDA*");
    delay(500);
    postelamed == 25; 
    inicio_lcd();
}
if (position == 4) // altera estado da porta  
{
    lcd.clear();
    lcd.setCursor(1, 1);
    lcd.setFontSize(FONT_SIZE_MEDIUM); 
    lcd.print("PORTA ABERTA");
    digitalWrite(buzzer, HIGH);
    delay(tempoBuzz);
    digitalWrite(buzzer, LOW); // acionamento do buzzer ao apertar qualquer tecla
    digitalWrite(buzzer, HIGH);
    delay(tempoBuzz);
    digitalWrite(buzzer, LOW); // acionamento do buzzer ao apertar qualquer tecla
    digitalWrite(buzzer, HIGH);
    delay(tempoBuzz);
    digitalWrite(buzzer, LOW); // acionamento do buzzer ao apertar qualquer tecla
digitalWrite(buzzer, LOW); // acionamento do buzzer ao apertar qualquer tecla
    digitalWrite(buzzer, HIGH);
    delay(tempoBuzz);
    digitalWrite(buzzer, LOW); // acionamento do buzzer ao apertar qualquer tecla
    digitalWrite(buzzer, HIGH);
    delay(tempoBuzz);
    digitalWrite(buzzer, LOW); // acionamento do buzzer ao apertar qualquer tecla
    abre_porta();
    inicio_lcd();


}
delay(100);
}
}

void inicio_lcd(){
    lcd.begin();
  lcd.clear();
  lcd.setCursor(50, 2);
  lcd.setFontSize(FONT_SIZE_MEDIUM);
  lcd.println("OLA!");
  lcd.setCursor(5, 5);
  lcd.setFontSize(FONT_SIZE_SMALL);
  lcd.println("Pressione uma tecla:");    

}

void abre_porta(){
  position = 0;
      digitalWrite(ledPin, LOW);
     delay(3000);
     digitalWrite(ledPin, HIGH);
     postelamed = 25; 
  
}
