# Fritzing sketch PRO (saved by Fritzing 0.9.3b)

parts:
  Part1 = Arduino Nano (Rev3.0) (ICSP)
  Part2 = Bluetooth HC-05 Macho
  Part3 = Bluetooth HC-05 Macho
  R1 = Basic Flex Resistor
  R2 = Basic Flex Resistor
  Part4 = InvenSense MPU6050
  Part5 = Arduino Nano (Rev3.0) (ICSP)
  Grove1 = Grove OLED 128x96
  U3 = LCD-16X2 [package=lcd-16x2_noholes]  # not connected
  R3 = Resistor [tolerance=±5% resistance=220 package="2010 [SMD]"]
  R4 = Resistor [tolerance=±5% resistance=220 package="2010 [SMD]"]
  R5 = Resistor [tolerance=±5% resistance=220 package="2010 [SMD]"]
  R6 = Resistor [tolerance=±5% resistance=220 package="2010 [SMD]"]
  R8 = Resistor [tolerance=±5% resistance=220 package="2010 [SMD]"]
  R9 = Resistor [tolerance=±5% resistance=220 package="2010 [SMD]"]

nets:
  N1: Part1.D3, Part2.TXD
  N2: Part1.D8, Part4.INT
  GND: Part1.GND, Part2.GND, Part4.GND, R3.Pin_1, R4.Pin_1, R6.Pin_1
  VCC: Part1.5V, Part2.VCC, R1.Pin_2, R2.Pin_2, Part4.VCC
  N3: Part1.A5, Part4.SCL
  N4: Part1.A4, Part4.SDA
  N5: Part1.A1, R1.pin_1, R4.Pin_0
  N6: Part1.A0, R2.pin_1, R3.Pin_0
  N7: Part2.RXD, R5.Pin_0
  N8: Part3.TXD, Part5.D3
  N9: Part3.RXD, R9.Pin_1
  VCC_2: Part3.VCC, Grove1.VCC
  GND_2: Part3.GND, Part5.GND, Grove1.GND, R9.Pin_0
  N10: Part5.D2, R8.Pin_1
  N11: Part5.A5, Grove1.SCL
  N12: Part5.A4, Grove1.SDA
