# Fritzing sketch Personal Weather Station (saved by Fritzing 0.9.3b)
breadboards: 1

parts:
  Part1 = Arduino Uno (Rev3)
  LCD1 = LCD screen
  DHT1 = DHT11 Humitidy and Temperature Sensor
  Part2 = GUVA-S12SD UV Light Sensor
  MQ-135_Breakout2 = Gas Sensor Breakout Board  # not connected
  buz1 = Piezo Buzzer
  U1 = POT [package=pot_mammoth]
  R1 = Resistor [tolerance=±5% resistance=220 package="2512 [SMD]"]
  R2 = Resistor [tolerance=±5% resistance=220 package="2512 [SMD]"]

nets:
  N1: Part1.A1, Part2.Out
  N2: Part1.D8, DHT1.DATA, R2.Pin_1
  N3: Part1.D10_PWM/SS, buz1.pin_2
  N4: Part1.D11_PWM/MOSI, LCD1.E
  N5: Part1.D12/MISO, LCD1.RS
  N6: Part1.D2, LCD1.DB7
  N7: Part1.D3_PWM, LCD1.DB6
  N8: Part1.D4, LCD1.DB5
  N9: Part1.D5_PWM, LCD1.DB4
  5V: Part1.5V, LCD1.VDD, DHT1.VDD, Part2.5V, buz1.pin_1, U1.E, R1.Pin_0, R2.Pin_0
  GND: Part1.GND, LCD1.VSS, LCD1.R/W, LCD1.LED-, DHT1.GND, Part2.GND, U1.S
  N10: LCD1.V0, U1.A
  N11: LCD1.LED+, R1.Pin_1

notes:
  Sensors: DHT11, UVM-30A and MQ-135
  Others: Passive Buzzer, Potentiometer and LCD 16x2
  Schematics by Oliver Kuy
  December 2019

custom parts:
  DHT11 Humitidy and Temperature Sensor: DHT11 Humidity and Temperature Sensor
  GUVA-S12SD UV Light Sensor: Extend your light-sensing spectrum with this analog UV sensor module. It uses a UV photodiode, which can detect the 240-370nm range of light (which covers UVB and most of UVA spectrum). The signal level from the photodiode is very small, in the nano-ampere level, so we tossed on an opamp to amplify the signal to a more manageable volt-level.
  Gas Sensor Breakout Board: Gas sensor breakout board. Input voltage is 5V. Sensor output is available in analog and digital.
  Piezo Buzzer: Part from https://www.nutsvolts.com/magazine/article/november2012_SmileysWorkshop modified to be .3 in spacing to match the adafruit buzzer 5V breadboard friendly part.

// code stored in the sketch: Personal Weather Station.ino
// --Library-- / Bibliotheken
  #include <LiquidCrystal.h>
  #include <DHT.h>
  #include <DHT_U.h>
  
// Sensor DHT-11 (DHT-11 Temperature and Humidity Sensor)
  #define DHTPIN 8
  #define DHTTYPE DHT11

//Declare Sensor

// LCD Display (PIN)(LCD1602 Module)
  LiquidCrystal lcd(12, 11, 5, 4, 3, 2);
  DHT dht(DHTPIN, DHTTYPE);

void setup() {
// Serial Monitor
  Serial.begin(9600);

// Buzzer
  pinMode (10, OUTPUT);  

// LCD Display
  lcd.begin(16, 2);
  lcd.setCursor(7,1);
  dht.begin();
  
// LCD Display (Temp and Humidity)
  lcd.setCursor(0,0);
  lcd.print("TMP:");
  lcd.setCursor(0,1);
  lcd.print("HMD:");
  lcd.setCursor(9,0);
  lcd.print("AIR:");
  lcd.setCursor(9,1);
  lcd.print("UVi:");
  }

void loop() {
  lcd.setCursor(6,1);
  lcd.print("%");
  lcd.setCursor(7,0);
  lcd.print("C");
  lcd.setCursor(6,0);
  lcd.print((char)223);
  lcd.setCursor(15,0);
  lcd.print("%");

// -- Temp and Humidity --
// Temp = Temperature in Fahrenheit and Humid = Humidity
    int f = dht.readHumidity();
    float c = dht.readTemperature(true);
    float ppm = analogRead(A0);
    int perppm = (ppm/300)*100;
    int revper = 100-perppm;
    int uvi = analogRead(A1);
    int temp = ((c-32)*5/9);

  // Sensor Error (For Example No Sensor)
    if (isnan(f) && (c) || isnan(ppm) || isnan(uvi)) {
      lcd.clear();
      lcd.setCursor(4,1);
      lcd.print("|SENSOR|");
      lcd.setCursor(4,0);
      lcd.print("|ERROR |");  
      delay(1000);
      return;
      }

// LCD Display (values)
  lcd.setCursor(4,0);
  lcd.print(temp);
  lcd.setCursor(4,1);
  lcd.print(f);
  lcd.setCursor(13,0);
  lcd.print(revper);
  lcd.setCursor(13,1);
  lcd.print(uvi);

  // Reading Warning
    if (temp >= 38 || temp <= 10 || f >= 85 || revper < 85 || uvi >= 9) {
        digitalWrite (10, HIGH);
        delay (200);
        digitalWrite (10, LOW);
        delay (200);
        digitalWrite (10, HIGH);
        delay (200);
        digitalWrite (10, LOW);
        delay (300000); 
    }
}
