# Fritzing sketch ROMAN_Raspi_with__Sound_sensor (saved by Fritzing 0.9.4)
breadboards: 1

parts:
  Raspberry_Pi_1 = Raspberry Pi 3 [part_number=RPI-3-V1.2]
  FC-1 = Sound Sensor

nets:
  N1: Raspberry_Pi_1.GPIO4, FC-1.OUT
  GND: Raspberry_Pi_1.GND, FC-1.GND
  5V: Raspberry_Pi_1.5V, FC-1.VCC
