# Fritzing sketch RS232 (saved by Fritzing 0.9.3b)
circuit board: 8.46667cm x 5.64444cm
breadboards: 1

parts:
  C1 = Electrolytic Capacitor [capacitance=10µF package="100 mil [THT, electrolytic]"]
  C3 = Electrolytic Capacitor [capacitance=10µF package="100 mil [THT, electrolytic]"]
  C5 = Electrolytic Capacitor [capacitance=10µF package="100 mil [THT, electrolytic]"]
  CN1 = DB9
  U1 = RS232 Transceiver [package=dil16]
  Part1 = Arduino Uno (Rev3)
  C2 = Electrolytic Capacitor [capacitance=10µF package="100 mil [THT, electrolytic]"]
  C4 = Electrolytic Capacitor [capacitance=10µF package="100 mil [THT, electrolytic]"]

nets:
  GND: C1.-, C5.+, CN1.5_GND, U1.GND, Part1.GND
  VCC: C1.+, U1.VCC, Part1.5V, C4.-
  N1: C3.-, U1.C2-
  N2: C3.+, U1.C2+
  N3: C5.-, U1.V-
  N4: CN1.2_RXD, U1.R2IN
  N5: CN1.3_TXD, U1.T2OUT
  N6: U1.C1+, C2.+
  N7: U1.V+, C4.+
  N8: U1.C1-, C2.-
  N9: U1.R2OUT, Part1.D10_PWM/SS
  N10: U1.T2IN, Part1.D11_PWM/MOSI

custom parts:
  DB9: RS232 connector, 9-pin, right-angle female. Minimum connections is RXD, TXD, GND

// code stored in the sketch: Scale_communication.ino
#include <SoftwareSerial.h>
#include "Timer.h"

SoftwareSerial mySerial(10, 11); // RX, TX
Timer t;

void setup() {
  // Open serial communications and wait for port to open:
  Serial.begin(9600);
  while (!Serial) {
    ; // wait for serial port to connect. Needed for native USB port only
  }

  
  //Serial.println("Goodnight moon!");

  // set the data rate for the SoftwareSerial port
  mySerial.begin(9600);
  t.every(1000,callScale);
  pinMode(13,OUTPUT);
  digitalWrite(13,LOW);
}

void loop() { // run over and over 
  t.update();
  
  
  if (mySerial.available()) {
    Serial.write(mySerial.read());
  }
  //if (Serial.available()) {
    //mySerial.write(Serial.read());
  //}
}

void callScale(){
  
  mySerial.write('S');
  mySerial.write('I');
  mySerial.write(13);
  mySerial.write(10);
}
