# Fritzing sketch Smart-Door-Lock (saved by Fritzing 0.9.3b)

parts:
  U1 = NodeMCU V1.0
  J1 = Piezo Speaker
  KY-1 = Keyes Relay [package=THT]
  M1 = DC Motor
  GT-511C1R1 = GT-511C1R Fingerprint Scanner

nets:
  N1: U1.D1, KY-1.signal
  N2: U1.D2, J1.pin2
  3V3: U1.3V3, GT-511C1R1.Vin
  GND: U1.GND, KY-1.ground, GT-511C1R1.GND
  N3: U1.D5, GT-511C1R1.Rx
  N4: U1.D6, GT-511C1R1.Tx
  N5: U1.Vin, KY-1.power
  N6: KY-1.NO, M1.pin_1

notes:
  12V Power
  Supply
  Solenoid Lock

custom parts:
  NodeMCU V1.0: ESP8266 based NodeMCU
  Keyes Relay: The Keyes 5V relay module is suitable for SCM development, home appliance control. It uses a 5V~12V TIL control signal which can control DC / AC signal.
  GT-511C1R Fingerprint Scanner: The GT-511C1R fingerprint scanner. The fingerprint module is produced by ADH-Tech. The GT-511C1 is based around the ARM Cortex M3 and can store 20 fingerprints.
