# Fritzing sketch StepperDriverMk1 (saved by Fritzing 0.9.3b)
circuit board: 7.7526cm x 5.81986cm
breadboards: 1

parts:
  DRV_2 = DRV 8825 Stepper Motor Carrier, High Current [part_number="DRV 8825"]
  C1 = Electrolytic Capacitor [capacitance=220µF voltage=16V package="200 mil [THT, electrolytic]"]
  C2 = Electrolytic Capacitor [capacitance=220µF voltage=16V package="200 mil [THT, electrolytic]"]
  IC1 = IC, DIP package, 36 pins [chip_label="Heltec WiFi32"]
  DRV_1 = DRV 8825 Stepper Motor Carrier, High Current [part_number="DRV 8825"]
  V1 = DC Power [voltage=5]
  SOT-223-3 = V_REG_MIC2920 [package=sot223]
  Pad10 = Pad [width=1.787407407407406 height=1.8814814814814806 connect=center]
  Pad8 = Pad [width=1.787407407407406 height=1.8814814814814806 connect=center]
  Pad7 = Pad [width=1.787407407407406 height=1.8814814814814806 connect=center]
  Pad6 = Pad [width=1.787407407407406 height=1.8814814814814806 connect=center]
  Pad5 = Pad [width=1.787407407407406 height=1.8814814814814806 connect=center]
  Pad4 = Pad [width=1.787407407407406 height=1.8814814814814806 connect=center]
  Pad3 = Pad [width=1.787407407407406 height=1.8814814814814806 connect=center]
  Pad2 = Pad [width=1.787407407407406 height=1.8814814814814806 connect=center]
  Pad1 = Pad [width=1.787407407407406 height=1.8814814814814806 connect=center]

nets:
  N1: DRV_2.MS1, IC1.pin10, DRV_1.MS1
  N2: DRV_2.MS2, IC1.pin9, DRV_1.MS2
  N3: DRV_2.MS3, IC1.pin8, DRV_1.MS3
  N4: DRV_2.RESET, DRV_2.SLEEP, IC1.pin7, DRV_1.RESET, DRV_1.SLEEP
  N5: DRV_2.STEP, IC1.pin12
  N6: DRV_2.DIRECTION, IC1.pin11
  N7: DRV_2.VOLTAGE_ST/_MT, C1.+, C2.+, DRV_1.VOLTAGE_ST/_MT, V1.V+, SOT-223-3.IN, Pad10.pad
  GND: DRV_2.GROUND_ST/_MT, DRV_2.GROUND_LOG, C1.-, C2.-, IC1.pin1, IC1.pin36, DRV_1.GROUND_ST/_MT, DRV_1.GROUND_LOG, V1.V-, SOT-223-3.GND
  N8: DRV_2.OUT_2B, Pad7.pad
  N9: DRV_2.OUT_2A, Pad5.pad
  N10: DRV_2.OUT_1A, Pad6.pad
  N11: DRV_2.OUT_1B, Pad8.pad
  N12: IC1.pin5, DRV_1.DIRECTION
  N13: IC1.pin6, DRV_1.STEP
  N14: IC1.pin35, SOT-223-3.OUT
  N15: DRV_1.OUT_2B, Pad3.pad
  N16: DRV_1.OUT_2A, Pad2.pad
  N17: DRV_1.OUT_1A, Pad1.pad
  N18: DRV_1.OUT_1B, Pad4.pad

notes:
  12V Sup
  StepperBoard Mk1 MSS
  +
