# Fritzing sketch Thermocouple (1) (saved by Fritzing 0.9.3b)

parts:
  Main = Arduino Uno (Rev3) [part_number=1]
  LCD1 = LCD screen [part_number=2]
  U1 = POT [package=pot_alpha_rv16af-20]
  U2 = MAX6675 [package=so08]

nets:
  N1: Main.D8, U2.SCK
  N2: Main.D11_PWM/MOSI, LCD1.E
  N3: Main.D12/MISO, LCD1.RS
  N4: Main.D2, LCD1.DB7
  N5: Main.D3_PWM, LCD1.DB6
  N6: Main.D4, LCD1.DB5
  N7: Main.D5_PWM, LCD1.DB4
  N8: Main.D6_PWM, U2.MISO
  N9: Main.D7, U2.CS
  N10: LCD1.VSS, U1.A
  N11: LCD1.VDD, U1.E
  N12: LCD1.V0, U1.S

notes:
  **Pin 2 and 3 requires a type K Thermocopule (TC) sensor**
  Pin 2: TC minus input
  Pin 3: TC plus input

// code stored in the sketch: Thermocopule.ino
#include <Wire.h>
#include <max6675.h>

#include <LiquidCrystal.h> 

#define RS 12
#define RW 11
#define D4 5
#define D5 4
#define D6 3
#define D7 2
 
LiquidCrystal lcd(RS, RW, D4, D5, D6, D7);

//////////////////

int termoSO = 6;
int termoCS = 7;
int termoCLK = 8;
 
MAX6675 thermocouple(termoCLK, termoCS, termoSO);

///////////

int vccPin = 3;
int gndPin = 2;
 
int amostragem = 10;

void setup() {
 lcd.begin(16, 2);
 lcd.print("--Termopar--");

  Serial.begin(9600);
  pinMode(vccPin, OUTPUT); digitalWrite(vccPin, HIGH);
  pinMode(gndPin, OUTPUT); digitalWrite(gndPin, LOW);
}

void loop() {
  float temperatura = 0;
   
   //Inicia a leituira das amostra
   for(int index =0; index < amostragem; index++){
     temperatura = thermocouple.readCelsius() + temperatura;
     delay(200);
   }
   
   temperatura = temperatura / amostragem;
   
   Serial.print("C = ");
   Serial.println(temperatura);
   
   lcd.setCursor(0,0);
   
   lcd.clear();
   
   lcd.print("Temperatura:");
   lcd.setCursor(0,1);
   lcd.print(" ");
   lcd.print(temperatura);
   lcd.print(" Celsius");
   delay(1);
}
