# Fritzing sketch Tonuino_Molex (saved by Fritzing 0.9.4)
circuit board: 6.0837cm x 5.77086cm

parts:
  DFRobot_DFPlayer_Mini1 = DFRobot DFPlayer Mini [part_number=DFR0299]
  Part1 = Arduino Nano (Rev3.0)
  Headphones = molex pin header, 3 pins [form=molex]
  R1 = Resistor [tolerance=±5% resistance=1k package=THT]
  A0 = molex pin header, 2 pins [form=molex]
  A1 = molex pin header, 2 pins [form=molex]
  A2 = molex pin header, 2 pins [form=molex]
  A4 = molex pin header, 2 pins [form=molex]
  A5 = molex pin header, 2 pins [form=molex]
  A6 = molex pin header, 2 pins [form=molex]
  A7 = molex pin header, 2 pins [form=molex]
  D8 = molex pin header, 2 pins [form=molex]
  D5 = molex pin header, 2 pins [form=molex]
  D6 = molex pin header, 2 pins [form=molex]
  D7 = molex pin header, 2 pins [form=molex]
  Speaker = molex pin header, 2 pins [form=molex]
  RC522 = molex pin header, 8 pins [form=molex]
  A3 = molex pin header, 2 pins [form=molex]
  Batt = molex pin header, 2 pins [form=molex]
  Switch = molex pin header, 2 pins [form=molex]

nets:
  5V: DFRobot_DFPlayer_Mini1.VCC, Part1.5V, Switch.pin1
  DF_RX: DFRobot_DFPlayer_Mini1.RX, R1.Pin_1
  DF_TX: DFRobot_DFPlayer_Mini1.TX, Part1.D2
  DAC_R: DFRobot_DFPlayer_Mini1.DAC_R, Headphones.pin1
  DAC_L: DFRobot_DFPlayer_Mini1.DAC_L, Headphones.pin2
  SPK1: DFRobot_DFPlayer_Mini1.SPK_1, Speaker.pin1
  GND: DFRobot_DFPlayer_Mini1.GND-1, DFRobot_DFPlayer_Mini1.GND-2, Part1.GND, Headphones.pin3, A0.pin1, A1.pin1, A2.pin1, A4.pin1, A5.pin1, A6.pin1, A7.pin1, D8.pin1, D5.pin1, D6.pin1, D7.pin1, RC522.pin6, A3.pin1, Batt.pin2
  SPK2: DFRobot_DFPlayer_Mini1.SPK_2, Speaker.pin2
  BUSY: DFRobot_DFPlayer_Mini1.BUSY, Part1.D4
  N1: Part1.D3, R1.Pin_0
  D5: Part1.D5, D5.pin2
  D6: Part1.D6, D6.pin2
  D7: Part1.D7, D7.pin2
  D8: Part1.D8, D8.pin2
  RST: Part1.D9, RC522.pin7
  SDA: Part1.D10, RC522.pin1
  MOSI: Part1.D11/MOSI, RC522.pin3
  MISO: Part1.D12/MISO, RC522.pin4
  A7: Part1.A7, A7.pin2
  A6: Part1.A6, A6.pin2
  A5: Part1.A5, A5.pin2
  A4: Part1.A4, A4.pin2
  A3: Part1.A3, A3.pin2
  A2: Part1.A2, A2.pin2
  A1: Part1.A1, A1.pin2
  A0: Part1.A0, A0.pin2
  3.3V: Part1.3V3, RC522.pin8
  SCK: Part1.D13/SCK, RC522.pin2
  IRQ: RC522.pin5
  5VBatt: Batt.pin1, Switch.pin2
