# Fritzing sketch animatronic (saved by Fritzing 0.9.3b)
breadboards: 1

parts:
  U2 = LCD-16X2 [package=lcd-16x2]
  Yellow_Indecator = LED - 5mm [color="Red (633nm)" package="5 mm [THT]"]
  Part1 = Adafruit T-Cobbler Plus [part_number="Adafruit #1989 and #2028"]
  PIR1 = PIR sensor
  R1 = Resistor [tolerance=±5% resistance=220 package="1206 [SMD]"]
  U3 = POT [package=pot_mammoth]
  S1 = Pushbutton [package="[THT]"]

nets:
  GND: U2.VSS, U2.R_W, U2.K, Part1.GND, PIR1.GND, R1.Pin_0, U3.E, S1.Pin_3, S1.Pin_4
  VDD: U2.VDD, U2.A, Part1.+5V, PIR1.VDD, U3.S
  N1: U2.VO, U3.A
  N2: U2.RS, Part1.GPIO27
  N3: U2.E, Part1.GPIO22
  N4: U2.DB4, Part1.GPIO25
  N5: U2.DB5, Part1.GPIO24
  N6: U2.DB6, Part1.GPIO23
  N7: U2.DB7, Part1.GPIO18
  N8: Yellow_Indecator.cathode, R1.Pin_1
  N9: Yellow_Indecator.anode, Part1.GPIO16
  N10: Part1.GPIO4, PIR1.SIG
  N11: Part1.GPIO21, S1.Pin_1, S1.Pin_2

custom parts:
  Adafruit T-Cobbler Plus: The Raspberry Pi has landed on the Maker World like a 40-GPIO pinned, quad-USB ported, credit card sized bomb of DIY joy. And while you can use most of our great Model B accessories by hooking up our downgrade cable, its probably a good time to upgrade your set up and accessorize using all of the 40 pins. That's why we now carry the Assembled Adafruit Pi T-Cobbler Plus - Breakout + Cable for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
