# Fritzing sketch moc3021 ac load operat (saved by Fritzing 0.8.7b)
breadboards: 1

parts:
  IC1 = IC, DIP package, 6 pins [chip_label=moc3021]
  TP1 = TTP223 Touch Module [part_number=TTP223]
  R1 = Resistor [tolerance=±5% resistance=220 package=THT]
  5V_input = Power plug
  230V_50HZ = Screw terminal - 2 pins [package=THT]
  Lamp = LEDs [package=led10mm]

nets:
  N1: IC1.pin1, R1.Pin_0
  GND: IC1.pin2, TP1.GND, 5V_input.GND
  N2: IC1.pin4, 230V_50HZ.pin2
  N3: IC1.pin6, Lamp.A
  N4: TP1.I/O, R1.Pin_1
  VCC: TP1.VCC, 5V_input.VCC
  N5: 230V_50HZ.pin1, Lamp.C

custom parts:
  TTP223 Touch Module: Single touch module. Other side has "A" "B" terminal to short and use "AHLB" & "Toggle" Mode.
  LEDs: LEDs Standard schematic elements and footprints for 5mm, 3mm, 1206, and 0603 sized LEDs. 5mm - Spark Fun Electronics SKU : COM-00529 (and others)
