# Fritzing sketch primer proyecto (saved by Fritzing 0.9.3b)
breadboards: 1

parts:
  Componente1 = Arduino Uno (Rev3)
  ZS-042_RTC1 = ZS-042 RTC Module
  KY-1 = Keyes Relay [package=THT]
  LED1 = LED - 5mm [color="Red (633nm)" package="5 mm [THT]"]
  LCD1 = LCD screen
  LCM1602_IIC1 = LCM1602 IIC [part_number="LCM1602 IIC" chip_label="LCM1602 IIC" package="DIP (Dual Inline) [THT]"]
  DHT1 = DHT22 Humidity and Temperature Sensor
  KY-2 = Keyes Relay [package=THT]
  KY-3 = Keyes Relay [package=THT]
  KY-4 = Keyes Relay [package=THT]
  DC-808_Water_Pump1 = DC-808 Water Pump
  J3 = Power Jack [package=power_jack_pth_lock]
  J1 = Generic male header - 3 pins [form="♂ (male)" package=THT]  # not connected
  Componente2 = FC-28 Soil Hygrometer Module - Probe  # not connected
  Componente3 = FC-28 Soil Hygrometer Module
  J2 = Generic male header - 3 pins [form="♂ (male)" package=THT]

nets:
  N1: Componente1.A0, Componente3.AO
  N2: Componente1.A4/SDA, LCM1602_IIC1.SCL
  N3: Componente1.D3_PWM, DHT1.DATA
  N4: Componente1.D5_PWM, KY-3.signal
  3V3: Componente1.3V3, DHT1.VDD
  5V: Componente1.5V, ZS-042_RTC1.VCC
  GND: Componente1.GND, ZS-042_RTC1.GND, DHT1.GND
  N5: KY-1.C, LED1.cathode
  N6: KY-1.NO, KY-2.NO, KY-3.NO, KY-4.NO, J3.GNDBREAK
  VDD: LCD1.VDD, LCM1602_IIC1.VDD
  N7: LCD1.V0, LCM1602_IIC1.V0
  N8: LCD1.RS, LCM1602_IIC1.RS
  N9: LCD1.R/W, LCM1602_IIC1.RW
  N10: LCD1.E, LCM1602_IIC1.E
  N11: LCD1.DB0, LCM1602_IIC1.D0
  N12: LCD1.DB1, LCM1602_IIC1.D1
  N13: LCD1.DB2, LCM1602_IIC1.D2
  N14: LCD1.DB3, LCM1602_IIC1.D3
  N15: LCD1.DB4, LCM1602_IIC1.D4
  N16: LCD1.DB5, LCM1602_IIC1.D5
  N17: LCD1.DB6, LCM1602_IIC1.D6
  N18: LCD1.DB7, LCM1602_IIC1.D7
  N19: LCD1.LED+, LCM1602_IIC1.A
  N20: LCD1.LED-, LCM1602_IIC1.K
  N21: KY-2.C, DC-808_Water_Pump1.VCC
  N22: KY-3.C, J2.pin1
  GND_2: DC-808_Water_Pump1.GND, J3.GND, J2.pin2

notes:
  TIERRA 220V
  BOMBA AGUA 220V
  FAN 1 IN 220v
  FAN2 IN 220v
  RELAY 4
  RELAY 1
  TEMPERATURA TIERRA
  LCD TEMP + HUME
  DS3231 GUARDA HORA
  dht22
  LAMPARA 220V

custom parts:
  Keyes Relay: The Keyes 5V relay module is suitable for SCM development, home appliance control. It uses a 5V~12V TIL control signal which can control DC / AC signal.
  LCM1602 IIC: I2C-Module to use a 1602 or 2004 LCD on with the wire.h libory Serial LCD Modul
  DC-808 Water Pump: Water pump.
  Generic male header - 3 pins: Generic male header
  FC-28 Soil Hygrometer Module - Probe: The FC-28 is a soil hygrometer module that uses the Texas Instruments LM393 comparator chip to provide an analog measurement of soil humidity.
  FC-28 Soil Hygrometer Module: The FC-28 is a soil hygrometer module that uses the Texas Instruments LM393 comparator chip to provide an analog measurement of soil humidity. The digital output is high when soil moisture is over a certain threshold, as determined by adjusting the potentiometer.

// code stored in the sketch: primer proyecto.fzz.ino
#include <DS3231.h>

int Relay = 4;

DS3231  rtc(SDA, SCL);
Time t;

const int OnHour = 12;
const int OnMin = 24;
const int OffHour = 12;
const int OffMin = 25;

void setup() {
  Serial.begin(115200);
  rtc.begin();
  pinMode(Relay, OUTPUT);
  digitalWrite(Relay, LOW);
}

void loop() {
  t = rtc.getTime();
  Serial.print(t.hour);
  Serial.print(" hour(s), ");
  Serial.print(t.min);
  Serial.print(" minute(s)");
  Serial.println(" ");
  delay (1000);
  
  if(t.hour == OnHour && t.min == OnMin){
    digitalWrite(Relay,HIGH);
    Serial.println("LIGHT ON");
    }
    
    else if(t.hour == OffHour && t.min == OffMin){
      digitalWrite(Relay,LOW);
      Serial.println("LIGHT OFF");
    }
}
