# Fritzing sketch sensor_gas (saved by Fritzing 0.9.2b)
circuit board: 8.46667cm x 5.64444cm
breadboards: 1

parts:
  U1 = Spark Core (v1.0)
  R1 = Resistor [tolerance=±5% resistance=4.7k package=THT]
  VCC1 = 4 x AAA Battery Mount
  J1 = Piezo Speaker
  U2 = GAS_SENSOR [package=mq-3]

nets:
  N1: U1.A2, U1.3V3, R1.Pin_1, U2.B1
  N2: U1.A3, U1.A6
  N3: U1.A5, U1.VIN, VCC1.+, U2.A1, U2.H1
  N4: U1.GND, R1.Pin_0, VCC1.-, J1.pin1, U2.H2
  N5: U1.D2, J1.pin2

notes:
  Black = Negative
  Red = Positive

custom parts:
  Spark Core (v1.0): The Spark Core is a tiny Wi-Fi development board that makes it easy to create internet-connected hardware. The Core is all you need to get started; power it over USB and in minutes you'll be controlling LEDs, switches and motors and collecting data from sensors over the internet! It has 8 digital I/O pins, 8 analog I/O pins, 8 PWM pins; UART (Serial), SPI, I2C, and JTAG peripherals available.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

// code stored in the sketch: sensor_gas.ino
int buzzerPin = D2;
int sensorPin = A2;
int valorSensor = 0;
int limit = 1300;

void setup() {
    pinMode(buzzerPin, OUTPUT);
    //pinMode(sensorPin, INPUT);
    Serial.begin(9600);
    Particle.variable("valorSensor", valorSensor);
}

void loop() {
    valorSensor = analogRead(sensorPin);
    Serial.println("Valor atual: ");
    Serial.println(valorSensor);
    delay(1000);
    gasAlarm();
}

void gasAlarm() {
    if (valorSensor > limit) { //buzzer goes off
        digitalWrite(buzzerPin, HIGH);
        delay(200);
        digitalWrite(buzzerPin, LOW);
        delay(200);
    }
    else {
        digitalWrite(buzzerPin, LOW);
    }
}
