# Fritzing sketch tid stage 2 (saved by Fritzing 0.9.2b)
breadboards: 1

parts:
  U1 = RS232 Transceiver [package=dil16]
  X1 = DB9 Connector [package=db9]
  Part1 = Arduino Uno (Rev3)
  C1 = Electrolytic Capacitor [capacitance=1µF package="100 mil [THT, electrolytic]"]
  C2 = Electrolytic Capacitor [capacitance=1µF package="100 mil [THT, electrolytic]"]

nets:
  N1: U1.C1+, C1.+
  GND: U1.V+, U1.V-, U1.GND, X1.5, Part1.GND
  N2: U1.C1-, C1.-
  N3: U1.C2+, C2.+
  N4: U1.C2-, C2.-
  N5: U1.T1IN, Part1.D1/TX
  N6: U1.R1IN, X1.3
  N7: U1.T1OUT, X1.1
  VCC: U1.VCC, Part1.5V

// code stored in the sketch: ProjectCode.ino
void setup(){
	pinMode(13, OUTPUT);
}

void loop(){
	digitalWrite(13, HIGH);
	delay(1000);
	digitalWrite(13, LOW);
	delay(1000);
}
