# Fritzing sketch rpi-4b-test-Sketch (saved by Fritzing 0.9.4)
circuit board: 12cm x 10cm

parts:
  Mod1 = Raspberry Pi 4B
  J2 = female pin header, 20 pins [form="♀ (female)"]
  J3 = female pin header, 20 pins [form="♀ (female)"]
  J4 = female pin header, 3 pins [form="♀ (female)"]
  J5 = female pin header, 2 pins [form="♀ (female)"]
  J6 = female pin header, 2 pins [form="♀ (female)"]

nets:
  N1: Mod1.3V3, J3.pin1, J3.pin9
  N2: Mod1.5V, J2.pin1, J2.pin2
  N3: Mod1.GPIO2, J3.pin2
  N4: Mod1.GPIO3, J3.pin3
  N5: Mod1.GND, J2.pin3, J2.pin7, J2.pin10, J2.pin15, J2.pin17, J3.pin5, J3.pin13, J3.pin20, J4.pin2
  N6: Mod1.GPIO4, J3.pin4
  N7: Mod1.GPIO14, J2.pin4
  N8: Mod1.GPIO15, J2.pin5
  N9: Mod1.GPIO17, J3.pin6
  N10: Mod1.GPIO18, J2.pin6
  N11: Mod1.GPIO27, J3.pin7
  N12: Mod1.GPIO22, J3.pin8
  N13: Mod1.GPIO23, J2.pin8
  N14: Mod1.GPIO24, J2.pin9
  N15: Mod1.GPIO10, J3.pin10
  N16: Mod1.GPIO9, J3.pin11
  N17: Mod1.GPIO25, J2.pin11
  N18: Mod1.GPIO11, J3.pin12
  N19: Mod1.GPIO8, J2.pin12
  N20: Mod1.GPIO7, J2.pin13
  N21: Mod1.ID_SD, J3.pin14
  N22: Mod1.ID_SC, J2.pin14
  N23: Mod1.GPIO5, J3.pin15
  N24: Mod1.GPIO6, J3.pin16
  N25: Mod1.GPIO12, J2.pin16
  N26: Mod1.GPIO13, J3.pin17
  N27: Mod1.GPIO19, J3.pin18
  N28: Mod1.GPIO16, J2.pin18
  N29: Mod1.GPIO26, J3.pin19
  N30: Mod1.GPIO20, J2.pin19
  N31: Mod1.GPIO21, J2.pin20
  N32: Mod1.TR01_TAP, J5.pin2
  N33: Mod1.TR00_TAP, J5.pin1
  N34: Mod1.TR03_TAP, J6.pin2
  N35: Mod1.TR02_TAP, J6.pin1
  N36: Mod1.RUN, J4.pin1
  N37: Mod1.GLOBAL_EN, J4.pin3
