# Fritzing sketch AMEDBA_LCD2004 (saved by Fritzing 0.9.2b)
breadboards: 1

parts:
  Ameba1 = Ameba
  LCM1602_IIC3 = LCM1602 IIC [part_number="LCM1602 IIC" chip_label="LCM1602 IIC" package="DIP (Dual Inline) [THT]"]
  LCD4 = LCD 20x04

nets:
  N1: Ameba1.SCL, LCM1602_IIC3.SCL
  N2: Ameba1.SDA, LCM1602_IIC3.SDA
  GND: Ameba1.GND, LCM1602_IIC3.GND
  5V: Ameba1.5V, LCM1602_IIC3.VCC
  VSS: LCM1602_IIC3.VSS, LCD4.VSS
  VDD: LCM1602_IIC3.VDD, LCD4.VDD
  N3: LCM1602_IIC3.V0, LCD4.V0
  N4: LCM1602_IIC3.RS, LCD4.RS
  N5: LCM1602_IIC3.RW, LCD4.R/W
  N6: LCM1602_IIC3.E, LCD4.E
  N7: LCM1602_IIC3.D0, LCD4.DB0
  N8: LCM1602_IIC3.D1, LCD4.DB1
  N9: LCM1602_IIC3.D2, LCD4.DB2
  N10: LCM1602_IIC3.D3, LCD4.DB3
  N11: LCM1602_IIC3.D4, LCD4.DB4
  N12: LCM1602_IIC3.D5, LCD4.DB5
  N13: LCM1602_IIC3.D6, LCD4.DB6
  N14: LCM1602_IIC3.D7, LCD4.DB7
  N15: LCM1602_IIC3.A, LCD4.LED+
  N16: LCM1602_IIC3.K, LCD4.LED-
  N17: LCM1602_IIC3.LED_A, LCM1602_IIC3.LED_B

custom parts:
  Ameba: Ameba EVB
  LCM1602 IIC: I2C-Module to use a 1602 or 2004 LCD on with the wire.h libory Serial LCD Modul
  LCD 20x04: LCD character display, 20 characters by 4 rows. Green.
