# Fritzing sketch Ameba_4Led (saved by Fritzing 0.9.2b)
breadboards: 1

parts:
  Ameba1 = Ameba
  R1 = Resistor [tolerance=±5% resistance=220 package=THT]
  LED1 = LED - 5mm [color="Red (633nm)" package="5 mm [THT]"]
  R2 = Resistor [tolerance=±5% resistance=220 package=THT]
  LED2 = LED - 5mm [color="Red (633nm)" package="5 mm [THT]"]
  R3 = Resistor [tolerance=±5% resistance=220 package=THT]
  LED3 = LED - 5mm [color="Red (633nm)" package="5 mm [THT]"]
  R4 = Resistor [tolerance=±5% resistance=220 package=THT]
  LED4 = LED - 5mm [color="Red (633nm)" package="5 mm [THT]"]

nets:
  N1: Ameba1.D8, R3.Pin_1
  N2: Ameba1.D10, R2.Pin_1
  N3: Ameba1.D11, R1.Pin_1
  N4: Ameba1.D12, R4.Pin_1
  N5: Ameba1.GND, LED1.cathode, LED2.cathode, LED3.cathode, LED4.cathode
  N6: R1.Pin_0, LED1.anode
  N7: R2.Pin_0, LED2.anode
  N8: R3.Pin_0, LED3.anode
  N9: R4.Pin_0, LED4.anode

custom parts:
  Ameba: Ameba EVB
