# Fritzing sketch Ameba_4x4KeyPad (saved by Fritzing 0.9.2b)
breadboards: 1

parts:
  Ameba1 = Ameba
  Matrix_keypad1 = KEYPAD 4x4

nets:
  N1: Ameba1.D5, Matrix_keypad1.row4
  N2: Ameba1.D6, Matrix_keypad1.row3
  N3: Ameba1.D7, Matrix_keypad1.row2
  N4: Ameba1.D8, Matrix_keypad1.row1
  N5: Ameba1.D9, Matrix_keypad1.col4
  N6: Ameba1.D10, Matrix_keypad1.col3
  N7: Ameba1.D11, Matrix_keypad1.col2
  N8: Ameba1.D12, Matrix_keypad1.col1

custom parts:
  Ameba: Ameba EVB
  KEYPAD 4x4: Matrix keypad 16 buttons, 4 rows x 4 columns
