# Fritzing sketch Ameba_Button_INT (saved by Fritzing 0.9.2b)
breadboards: 1

parts:
  Ameba1 = Ameba
  Part2 = KY-004 Key Switch Module [package="Breakout board"]

nets:
  N1: Ameba1.D3, Part2.S
  N2: Ameba1.GND, Part2.-
  5V: Ameba1.5V, Part2.Vin

notes:
  Interrupt D3

custom parts:
  Ameba: Ameba EVB
  KY-004 Key Switch Module: Arduino Key Switch Module Keyes KY-004 is a push button that will output a high signal when pressed.
