# Fritzing sketch Ameba_DHT22 (saved by Fritzing 0.9.2b)
breadboards: 1

parts:
  Ameba1 = Ameba
  DHT1 = DHT22 Humidity and Temperature Sensor

nets:
  GND: Ameba1.GND, DHT1.GND
  5V: Ameba1.5V, DHT1.VDD

notes:
  DHT DataOut
  D7

custom parts:
  Ameba: Ameba EVB
