# Fritzing sketch Ameba_DHT22_HC-05 (saved by Fritzing 0.9.2b)
breadboards: 1

parts:
  Ameba1 = Ameba
  DHT1 = DHT22 Humidity and Temperature Sensor
  元件1 = Bluetooth HC-05 Macho

nets:
  N1: Ameba1.D0, 元件1.TXD
  N2: Ameba1.D1, 元件1.RXD
  GND: Ameba1.GND, DHT1.GND, 元件1.GND
  5V: Ameba1.5V, DHT1.VDD, 元件1.VCC

custom parts:
  Ameba: Ameba EVB
