# Fritzing sketch Ameba_HC-05 (saved by Fritzing 0.9.2b)
breadboards: 1

parts:
  Ameba1 = Ameba
  元件1 = Bluetooth HC-05 Macho

nets:
  N1: Ameba1.D0, 元件1.TXD
  N2: Ameba1.D1, 元件1.RXD
  GND: Ameba1.GND, 元件1.GND
  5V: Ameba1.5V, 元件1.VCC

custom parts:
  Ameba: Ameba EVB
