# Fritzing sketch Ameba_HC-SR04 (saved by Fritzing 0.9.2b)
breadboards: 1

parts:
  Ameba1 = Ameba
  元件1 = SRF05 Ultrasonic Rangefinder

nets:
  N1: Ameba1.D12, 元件1.Trig
  N2: Ameba1.D13, 元件1.Echo
  GND: Ameba1.GND, 元件1.GND
  5V: Ameba1.5V, 元件1.VCC

custom parts:
  Ameba: Ameba EVB
