# Fritzing sketch Ameba_LCD2004_MP3_DHT22_Button_INT (saved by Fritzing 0.9.2b)
breadboards: 1

parts:
  Ameba1 = Ameba
  LCM1602_IIC3 = LCM1602 IIC [part_number="LCM1602 IIC" chip_label="LCM1602 IIC" package="DIP (Dual Inline) [THT]"]
  LCD4 = LCD 20x04
  DFPlayer_Mini2 = DFPlayer MINI [package="DIP (Dual Inline) [THT]"]
  SP2 = SPEAKER [package=pcb_mount_speaker]
  SP3 = SPEAKER [package=pcb_mount_speaker]
  DHT2 = DHT22 Humidity and Temperature Sensor
  Part1 = KY-004 Key Switch Module [package="Breakout board"]

nets:
  N1: Ameba1.D3, Part1.S
  N2: Ameba1.D7, DHT2.DATA
  N3: Ameba1.D8, DFPlayer_Mini2.TX
  N4: Ameba1.D9, DFPlayer_Mini2.RX
  N5: Ameba1.SCL, LCM1602_IIC3.SCL
  N6: Ameba1.SDA, LCM1602_IIC3.SDA
  GND: Ameba1.GND, LCM1602_IIC3.GND, DFPlayer_Mini2.GND#9, DHT2.GND, Part1.-
  VCC: Ameba1.5V, LCM1602_IIC3.VCC, DFPlayer_Mini2.VCC, DHT2.VDD
  VSS: LCM1602_IIC3.VSS, LCD4.VSS
  VDD: LCM1602_IIC3.VDD, LCD4.VDD
  N7: LCM1602_IIC3.V0, LCD4.V0
  N8: LCM1602_IIC3.RS, LCD4.RS
  N9: LCM1602_IIC3.RW, LCD4.R/W
  N10: LCM1602_IIC3.E, LCD4.E
  N11: LCM1602_IIC3.D0, LCD4.DB0
  N12: LCM1602_IIC3.D1, LCD4.DB1
  N13: LCM1602_IIC3.D2, LCD4.DB2
  N14: LCM1602_IIC3.D3, LCD4.DB3
  N15: LCM1602_IIC3.D4, LCD4.DB4
  N16: LCM1602_IIC3.D5, LCD4.DB5
  N17: LCM1602_IIC3.D6, LCD4.DB6
  N18: LCM1602_IIC3.D7, LCD4.DB7
  N19: LCM1602_IIC3.A, LCD4.LED+
  N20: LCM1602_IIC3.K, LCD4.LED-
  N21: LCM1602_IIC3.LED_A, LCM1602_IIC3.LED_B
  N22: DFPlayer_Mini2.SPK1, SP3.-
  N23: DFPlayer_Mini2.GND#6, SP2.+, SP3.+
  N24: DFPlayer_Mini2.SPK2, SP2.-

notes:
  DHT DataOut
  D7
  LCD2004
  SDA (Yellow Line)
  SCL (Green Line)
  DF Mini Player
  Tx to D8, Rx to D9
  Interrupt D3

custom parts:
  Ameba: Ameba EVB
  LCM1602 IIC: I2C-Module to use a 1602 or 2004 LCD on with the wire.h libory Serial LCD Modul
  LCD 20x04: LCD character display, 20 characters by 4 rows. Green.
  DFPlayer MINI: MP3 module by DFRobot.com for playing Music from an SD-Card. Supports WAV and MP3 files.
  KY-004 Key Switch Module: Arduino Key Switch Module Keyes KY-004 is a push button that will output a high signal when pressed.
