# Fritzing sketch Ameba_Mp3 (saved by Fritzing 0.9.2b)
breadboards: 1

parts:
  Ameba1 = Ameba
  DFPlayer_Mini1 = DFPlayer MINI [package="DIP (Dual Inline) [THT]"]
  SP1 = SPEAKER [package=pcb_mount_speaker]
  SP2 = SPEAKER [package=pcb_mount_speaker]

nets:
  N1: Ameba1.D8, DFPlayer_Mini1.TX
  N2: Ameba1.D9, DFPlayer_Mini1.RX
  N3: Ameba1.GND, DFPlayer_Mini1.GND#9
  5V: Ameba1.5V, DFPlayer_Mini1.VCC
  N4: DFPlayer_Mini1.SPK1, SP1.-
  N5: DFPlayer_Mini1.GND#6, SP1.+, SP2.+
  N6: DFPlayer_Mini1.SPK2, SP2.-

notes:
  DF Mini Player
  Tx to D8, Rx to D9

custom parts:
  Ameba: Ameba EVB
  DFPlayer MINI: MP3 module by DFRobot.com for playing Music from an SD-Card. Supports WAV and MP3 files.
