# Fritzing sketch Ameba_PIR (saved by Fritzing 0.9.2b)
breadboards: 1

parts:
  Ameba1 = Ameba
  PIR1 = PIR sensor
  R1 = Resistor [tolerance=±5% resistance=220 package=THT]
  LED1 = LED - 5mm [color="Red (633nm)" package="5 mm [THT]"]

nets:
  N1: Ameba1.D8, PIR1.SIG
  N2: Ameba1.D13, R1.Pin_1
  GND: Ameba1.GND, PIR1.GND, LED1.cathode
  5V: Ameba1.5V, PIR1.VDD
  N3: R1.Pin_0, LED1.anode

custom parts:
  Ameba: Ameba EVB
