# Fritzing sketch Ameba_PIR_with_PowerLed (saved by Fritzing 0.9.2b)
breadboards: 1

parts:
  Ameba1 = Ameba
  PIR1 = PIR sensor
  R1 = Resistor [tolerance=±5% resistance=220 package=THT]
  LED1 = LED - 5mm [color="Green (565nm)" package="5 mm [THT]"]
  LED2 = LED - 5mm [color="Yellow (595nm)" package="5 mm [THT]"]
  R2 = Resistor [tolerance=±5% resistance=220 package=THT]

nets:
  N1: Ameba1.D8, PIR1.SIG
  N2: Ameba1.D12, R1.Pin_1
  N3: Ameba1.D13, R2.Pin_1
  GND: Ameba1.GND, PIR1.GND, LED1.cathode, LED2.cathode
  5V: Ameba1.5V, PIR1.VDD
  N4: R1.Pin_0, LED1.anode
  N5: LED2.anode, R2.Pin_0

custom parts:
  Ameba: Ameba EVB
