# Fritzing sketch Ameba_TFT22 (saved by Fritzing 0.9.2b)
breadboards: 1

parts:
  Ameba1 = Ameba
  TFT1 = 2.2" TFT with MicroSD Breakout

nets:
  GND: Ameba1.GND, TFT1.GND
  5V: Ameba1.5V, TFT1.VIN

custom parts:
  Ameba: Ameba EVB
  2.2" TFT with MicroSD Breakout: 2.2" TFT Display with HX8340B Controller and MicroSD Card
