# Fritzing sketch ameba基本電路(上)_4Leds (saved by Fritzing 0.9.2b)
breadboards: 1

parts:
  Ameba1 = Ameba
  LED1 = LED - 5mm [color="Red (633nm)" package="5 mm [THT]"]
  R1 = Resistor [tolerance=±5% resistance=220 package=THT]
  R2 = Resistor [tolerance=±5% resistance=220 package=THT]
  R3 = Resistor [tolerance=±5% resistance=220 package=THT]
  R4 = Resistor [tolerance=±5% resistance=220 package=THT]
  LED2 = LED - 5mm [color="Red (633nm)" package="5 mm [THT]"]
  LED3 = LED - 5mm [color="Red (633nm)" package="5 mm [THT]"]
  LED4 = LED - 5mm [color="Red (633nm)" package="5 mm [THT]"]

nets:
  N1: Ameba1.D10, R1.Pin_0
  N2: Ameba1.D11, R2.Pin_0
  N3: Ameba1.D12, R3.Pin_0
  N4: Ameba1.D13, R4.Pin_0
  N5: Ameba1.GND, LED1.cathode, LED2.cathode, LED3.cathode, LED4.cathode
  N6: LED1.anode, R1.Pin_1
  N7: R2.Pin_1, LED2.anode
  N8: R3.Pin_1, LED3.anode
  N9: R4.Pin_1, LED4.anode

custom parts:
  Ameba: Ameba EVB
