# Fritzing sketch ameba基本電路(上)_Relat2Led (saved by Fritzing 0.9.2b)
breadboards: 1

parts:
  Ameba1 = Ameba
  KY-1 = Keyes Relay [package=THT]
  LED1 = LED - 5mm [color="Red (633nm)" package="5 mm [THT]"]

nets:
  N1: Ameba1.D13, KY-1.signal
  N2: Ameba1.GND, KY-1.ground, LED1.cathode
  N3: Ameba1.5V, KY-1.power, KY-1.C
  N4: KY-1.NO, LED1.anode

custom parts:
  Ameba: Ameba EVB
  Keyes Relay: The Keyes 5V relay module is suitable for SCM development, home appliance control. It uses a 5V~12V TIL control signal which can control DC / AC signal.
