# Fritzing sketch ameba基本電路_ADS1115 (saved by Fritzing 0.9.2b)
breadboards: 1

parts:
  Ameba1 = Ameba
  元件1 = Adafruit ADS1115 16Bit I2C ADC [part_number="Adafruit #1085"]

nets:
  N1: Ameba1.SCL, 元件1.SCL
  N2: Ameba1.SDA, 元件1.SDA
  GND: Ameba1.GND, 元件1.GND
  5V: Ameba1.5V, 元件1.VDD

notes:
  Analog Input

custom parts:
  Ameba: Ameba EVB
  Adafruit ADS1115 16Bit I2C ADC: For microcontrollers without an analog-to-digital converter or when you want a higher-precision ADC, the ADS1115 provides 16-bit precision at 860 samples/second over I2C. The chip can be configured as 4 single-ended input channels, or two differential channels. As a nice bonus, it even includes a programmable gain amplifier, up to x16, to help boost up smaller single/differential signals to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
