# Fritzing sketch ameba基本電路_Blink(D13) (saved by Fritzing 0.9.2b)
breadboards: 1

parts:
  Ameba1 = Ameba
  LED1 = LED - 5mm [color="Red (633nm)" package="5 mm [THT]"]
  R1 = Resistor [tolerance=±5% resistance=220 package=THT]

nets:
  N1: Ameba1.D13, R1.Pin_1
  N2: Ameba1.GND, LED1.cathode
  N3: LED1.anode, R1.Pin_0

custom parts:
  Ameba: Ameba EVB
