# Fritzing sketch ameba基本電路_PS2搖桿_2LedPWM (saved by Fritzing 0.9.2b)
breadboards: 1

parts:
  Ameba1 = Ameba
  元件1 = Thumb Joystick
  part = Resistor [tolerance=±5% resistance=220 package=THT]
  part_2 = LED - 5mm [color="Red (633nm)" package="5 mm [THT]"]
  part_3 = Resistor [tolerance=±5% resistance=220 package=THT]
  part_4 = LED - 5mm [color="Green (560nm)" package="5 mm [THT]"]

nets:
  N1: Ameba1.D7, 元件1.SEL
  N2: Ameba1.D12, part_3.Pin_1
  N3: Ameba1.D13, part.Pin_1
  N4: Ameba1.A2, 元件1.HORZ
  N5: Ameba1.A1, 元件1.VERT
  GND: Ameba1.GND, 元件1.GND, part_2.cathode, part_4.cathode
  5V: Ameba1.5V, 元件1.VCC
  N6: part.Pin_0, part_2.anode
  N7: part_3.Pin_0, part_4.anode

notes:
  A2
  VRY
  A1
  VRX
  D7
  SW
  D13
  LED1
  D12
  LED2

custom parts:
  Ameba: Ameba EVB
