# Fritzing sketch ameba基本電路_PS2搖桿_Led12 (saved by Fritzing 0.9.2b)
breadboards: 1

parts:
  Ameba1 = Ameba
  元件1 = Thumb Joystick
  part = Resistor [tolerance=±5% resistance=220 package=THT]
  part_2 = LED - 5mm [color="Red (633nm)" package="5 mm [THT]"]

nets:
  N1: Ameba1.D7, 元件1.SEL
  N2: Ameba1.D13, part.Pin_1
  N3: Ameba1.A2, 元件1.HORZ
  N4: Ameba1.A1, 元件1.VERT
  GND: Ameba1.GND, 元件1.GND, part_2.cathode
  5V: Ameba1.5V, 元件1.VCC
  N5: part.Pin_0, part_2.anode

notes:
  A2
  VRY
  A1
  VRX
  D7
  SW
  D13
  LED1

custom parts:
  Ameba: Ameba EVB
