# Fritzing sketch ameba基本電路_測試按鈕通路 (saved by Fritzing 0.9.2b)
breadboards: 1

parts:
  Ameba1 = Ameba
  Mini_Button = Pushbutton [package="[THT]"]
  part = Resistor [tolerance=±5% resistance=220 package=THT]
  LED2 = LED - 5mm [color="Red (633nm)" package="5 mm [THT]"]

nets:
  N1: Ameba1.GND, LED2.cathode
  N2: Ameba1.5V, part.Pin_0
  N3: Mini_Button.Pin_1, Mini_Button.Pin_2
  N4: Mini_Button.Pin_3, Mini_Button.Pin_4, part.Pin_1, LED2.anode

custom parts:
  Ameba: Ameba EVB
