# Fritzing sketch ameba按鈕控制lED(PullDown) (saved by Fritzing 0.9.2b)
breadboards: 1

parts:
  Ameba1 = Ameba
  Mini_Button = Pushbutton [package="[THT]"]
  part = Resistor [tolerance=±5% resistance=220 package=THT]
  LED2 = LED - 5mm [color="Red (633nm)" package="5 mm [THT]"]
  R2 = Resistor [tolerance=±5% resistance=4.7k package=THT]

nets:
  N1: Ameba1.D7, Ameba1.GND, Mini_Button.Pin_3, Mini_Button.Pin_4, LED2.cathode, R2.Pin_1
  N2: Ameba1.D13, part.Pin_1
  N3: Ameba1.5V, R2.Pin_0
  N4: Mini_Button.Pin_1, Mini_Button.Pin_2
  N5: part.Pin_0, LED2.anode

custom parts:
  Ameba: Ameba EVB
