# Fritzing sketch ESP32-TTGO-T-DISPLAY_空白版 (saved by Fritzing 0.9.2b)
breadboards: 1

parts:
  Mod2 = ESP32-TTGO-T-DISPLAY
  YwRobot_Power_Supply1 = YwRobot Breadboard Power Supply [part_number=545043]

nets:
  N1: Mod2.G-1, Mod2.G-2, Mod2.G-10, Mod2.G-11, Mod2.G-14, YwRobot_Power_Supply1.GND#13, YwRobot_Power_Supply1.GND#14
  N2: YwRobot_Power_Supply1.VCC#5, YwRobot_Power_Supply1.VCC#6
  N3: YwRobot_Power_Supply1.VCC#9, YwRobot_Power_Supply1.VCC#10
  N4: YwRobot_Power_Supply1.GND#11, YwRobot_Power_Supply1.GND#12

custom parts:
  ESP32-TTGO-T-DISPLAY: LILYGO TTGO T-Display GD32VF103CBT6 Main Chip ST7789 1.14 Inch IPS 240x135 Resolution Minimalist Development Board.
  YwRobot Breadboard Power Supply: The YwRobot Breadboard Power Supply (MB-V2) has two power rails; they can be 5V or 3V3. Power to the module can be provided through the female USB socket or through the A10 (female) 2.1mm power jack.
