# Fritzing sketch ESP32S_BH1750_WS2812 (saved by Fritzing 0.9.2b)
breadboards: 1

parts:
  U1 = ESP32S-HiLetgo [part_number=ESP32S-HiLetgo]
  Part1 = BH1750
  U2 = WS2812 RGB LED matrix 4x4

nets:
  VCC: U1.3.3, Part1.VCC, U2.VCC
  GND: U1.GND, Part1.GND, U2.GND
  N1: U1.GPIO15, U2.DIN
  N2: U1.GPIO21, Part1.SDA
  N3: U1.GPIO22, Part1.SCL

custom parts:
  ESP32S-HiLetgo: HiLetgo ESP-WROOM-32 ESP32 ESP-32S Development Board 2.4GHz Dual-Mode WiFi + Bluetooth Dual Cores Microcontroller The ESP32 integrated with Antenna switches, RF Balun, power amplifiers, low-noise amplifiers, filters, and management modules, and the entire solution occupies the least area of PCB. 2.4 GHz Wi-Fi plus Bluetooth dual-mode chip, with TSMC Ultra-low power consumption 40nm technology,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
  BH1750: Light Sensor
  WS2812 RGB LED matrix 4x4: WS2812 matrix 4x4
