# Fritzing sketch ESP32S_MFC522 (saved by Fritzing 0.9.2b)
breadboards: 1

parts:
  U1 = ESP32S-HiLetgo [part_number=ESP32S-HiLetgo]
  Part1 = RFID-RC522-v2

nets:
  N1: U1.3.3, Part1.3.3V
  N2: U1.GPIO27, Part1.RST
  GND: U1.GND, Part1.GND
  N3: U1.GPIO5, Part1.SDA
  N4: U1.GPIO18, Part1.SCK
  N5: U1.GPIO19, Part1.MISO
  N6: U1.GPIO23, Part1.MOSI

custom parts:
  ESP32S-HiLetgo: HiLetgo ESP-WROOM-32 ESP32 ESP-32S Development Board 2.4GHz Dual-Mode WiFi + Bluetooth Dual Cores Microcontroller The ESP32 integrated with Antenna switches, RF Balun, power amplifiers, low-noise amplifiers, filters, and management modules, and the entire solution occupies the least area of PCB. 2.4 GHz Wi-Fi plus Bluetooth dual-mode chip, with TSMC Ultra-low power consumption 40nm technology,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
  RFID-RC522-v2: A simple China made RFID-RC522 Reader; do check the pin labels, as this is a MFRC522 based clone.
