# Fritzing sketch ESP32S_MPU6050 (saved by Fritzing 0.9.2b)
breadboards: 1

parts:
  U1 = ESP32S-HiLetgo [part_number=ESP32S-HiLetgo]
  MPU-1 = Adafruit MPU6050
  Part1 = Solid State High Level Relay Module [package=relay]  # not connected

nets:
  N1: U1.3.3, MPU-1.VCC
  GND: U1.GND, MPU-1.GND
  N2: U1.GPIO21, MPU-1.SDA
  N3: U1.GPIO22, MPU-1.SCL

custom parts:
  ESP32S-HiLetgo: HiLetgo ESP-WROOM-32 ESP32 ESP-32S Development Board 2.4GHz Dual-Mode WiFi + Bluetooth Dual Cores Microcontroller The ESP32 integrated with Antenna switches, RF Balun, power amplifiers, low-noise amplifiers, filters, and management modules, and the entire solution occupies the least area of PCB. 2.4 GHz Wi-Fi plus Bluetooth dual-mode chip, with TSMC Ultra-low power consumption 40nm technology,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
  Adafruit MPU6050: The MPU-6050 is a popular six axis accelerometer and gyroscope (gyro) that has all the info you need on how things are shakin' and spinnin' . With six axes of sensing and 16-bit measurements, you'll have everything you need to give your robot friend an inner ear. This combination of gyroscopes and accelerometers is commonly referred to as an Inertial Measurement Unit or IMU. Not so long ago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
  Solid State High Level Relay Module: 5V Omron solid state relay 240V 2A output with resistance fuse.
