# Fritzing sketch ESP32S_MQx (saved by Fritzing 0.9.2b)
breadboards: 1

parts:
  U1 = ESP32S-HiLetgo [part_number=ESP32S-HiLetgo]
  LCD2004-I2C1 = LCD2004-I2C
  U2 = GAS_SENSOR [package=mq-3]

nets:
  N1: U1.3.3, LCD2004-I2C1.VCC, U2.B1
  GND: U1.GND, LCD2004-I2C1.GND
  N2: U1.GPIO21, LCD2004-I2C1.SDA
  N3: U1.GPIO22, LCD2004-I2C1.SCL

custom parts:
  ESP32S-HiLetgo: HiLetgo ESP-WROOM-32 ESP32 ESP-32S Development Board 2.4GHz Dual-Mode WiFi + Bluetooth Dual Cores Microcontroller The ESP32 integrated with Antenna switches, RF Balun, power amplifiers, low-noise amplifiers, filters, and management modules, and the entire solution occupies the least area of PCB. 2.4 GHz Wi-Fi plus Bluetooth dual-mode chip, with TSMC Ultra-low power consumption 40nm technology,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
  LCD2004-I2C: A standard character display with 4x20 characters. Comes in many colors with LCM2004 IIC attached.
