# Fritzing sketch ESP32S_WS2812_4X4 (saved by Fritzing 0.9.2b)
breadboards: 1

parts:
  U1 = ESP32S-HiLetgo [part_number=ESP32S-HiLetgo]
  U2 = WS2812 RGB LED matrix 4x4

nets:
  N1: U1.3.3, U2.VCC
  GND: U1.GND, U2.GND
  N2: U1.GPIO4, U2.DIN

notes:
  WS2812B DIN
  GPIO 4

custom parts:
  ESP32S-HiLetgo: HiLetgo ESP-WROOM-32 ESP32 ESP-32S Development Board 2.4GHz Dual-Mode WiFi + Bluetooth Dual Cores Microcontroller The ESP32 integrated with Antenna switches, RF Balun, power amplifiers, low-noise amplifiers, filters, and management modules, and the entire solution occupies the least area of PCB. 2.4 GHz Wi-Fi plus Bluetooth dual-mode chip, with TSMC Ultra-low power consumption 40nm technology,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
  WS2812 RGB LED matrix 4x4: WS2812 matrix 4x4
