# Fritzing sketch ESP32_HMC5883L_Compass_LCD2004_I2C (saved by Fritzing 0.9.2b)
breadboards: 1

parts:
  U1 = ESP32S-HiLetgo [part_number=ESP32S-HiLetgo]
  LCD2004-I2C1 = LCD2004-I2C
  YwRobot_Power_Supply3 = YwRobot Breadboard Power Supply [part_number=545043]
  Module1 = Boladge HMC5883L Compass Module

nets:
  GND: U1.GND, LCD2004-I2C1.GND, YwRobot_Power_Supply3.GND#13, YwRobot_Power_Supply3.GND#14, Module1.GND
  N1: U1.GPIO21, LCD2004-I2C1.SDA, Module1.SDA
  N2: U1.GPIO22, LCD2004-I2C1.SCL, Module1.SCL
  VCC: LCD2004-I2C1.VCC, YwRobot_Power_Supply3.VCC#9, YwRobot_Power_Supply3.VCC#10, Module1.VCC
  N3: YwRobot_Power_Supply3.VCC#5, YwRobot_Power_Supply3.VCC#6
  N4: YwRobot_Power_Supply3.GND#11, YwRobot_Power_Supply3.GND#12

custom parts:
  ESP32S-HiLetgo: HiLetgo ESP-WROOM-32 ESP32 ESP-32S Development Board 2.4GHz Dual-Mode WiFi + Bluetooth Dual Cores Microcontroller The ESP32 integrated with Antenna switches, RF Balun, power amplifiers, low-noise amplifiers, filters, and management modules, and the entire solution occupies the least area of PCB. 2.4 GHz Wi-Fi plus Bluetooth dual-mode chip, with TSMC Ultra-low power consumption 40nm technology,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
  LCD2004-I2C: A standard character display with 4x20 characters. Comes in many colors with LCM2004 IIC attached.
  YwRobot Breadboard Power Supply: The YwRobot Breadboard Power Supply (MB-V2) has two power rails; they can be 5V or 3V3. Power to the module can be provided through the female USB socket or through the A10 (female) 2.1mm power jack.
  Boladge HMC5883L Compass Module: Cheap digital compass module
