# Fritzing sketch ESP32_HTU21D_OLED128x32 (saved by Fritzing 0.9.2b)
breadboards: 1

parts:
  U1 = ESP32S-HiLetgo [part_number=ESP32S-HiLetgo]
  YwRobot_Power_Supply3 = YwRobot Breadboard Power Supply [part_number=545043]
  OLED1 = 128x32 I2C Monochrome OLED Display
  元件2 = HTU21D-F Temperature + Humidity Sensor

nets:
  N1: U1.3.3, OLED1.3.3V
  GND: U1.GND, YwRobot_Power_Supply3.GND#13, YwRobot_Power_Supply3.GND#14, OLED1.GND, 元件2.GND
  N2: U1.GPIO21, OLED1.SDA, 元件2.SDA
  N3: U1.GPIO22, OLED1.SCL, 元件2.SCL
  N4: YwRobot_Power_Supply3.VCC#5, YwRobot_Power_Supply3.VCC#6
  N5: YwRobot_Power_Supply3.VCC#9, YwRobot_Power_Supply3.VCC#10, 元件2.VIN
  N6: YwRobot_Power_Supply3.GND#11, YwRobot_Power_Supply3.GND#12

custom parts:
  ESP32S-HiLetgo: HiLetgo ESP-WROOM-32 ESP32 ESP-32S Development Board 2.4GHz Dual-Mode WiFi + Bluetooth Dual Cores Microcontroller The ESP32 integrated with Antenna switches, RF Balun, power amplifiers, low-noise amplifiers, filters, and management modules, and the entire solution occupies the least area of PCB. 2.4 GHz Wi-Fi plus Bluetooth dual-mode chip, with TSMC Ultra-low power consumption 40nm technology,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
  YwRobot Breadboard Power Supply: The YwRobot Breadboard Power Supply (MB-V2) has two power rails; they can be 5V or 3V3. Power to the module can be provided through the female USB socket or through the A10 (female) 2.1mm power jack.
  HTU21D-F Temperature + Humidity Sensor: This I2C digital humidity sensor is an accurate and intelligent alternative to the much simpler Humidity and Temperature Sensor - SHT15 Breakout It has a typical accuracy of ±2% with an operating range that's optimized from 5% to 95% RH. Operation outside this range is still possible - just the accuracy might drop a bit. The temperature output has an accuracy of ±1°C from -30~90°C. If you're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
