# Fritzing sketch ESP32_LCD1602_DHT11 (saved by Fritzing 0.9.2b)
breadboards: 1

parts:
  LCM1602_IIC3 = LCM1602 IIC [part_number="LCM1602 IIC" chip_label="LCM1602 IIC" package="DIP (Dual Inline) [THT]"]
  LCD1 = LCD screen
  U1 = ESP32S-HiLetgo [part_number=ESP32S-HiLetgo]
  DHT1 = DHT11 Humitidy and Temperature Sensor

nets:
  VSS: LCM1602_IIC3.VSS, LCD1.VSS
  VDD: LCM1602_IIC3.VDD, LCD1.VDD
  N1: LCM1602_IIC3.V0, LCD1.V0
  N2: LCM1602_IIC3.RS, LCD1.RS
  N3: LCM1602_IIC3.RW, LCD1.R/W
  N4: LCM1602_IIC3.E, LCD1.E
  N5: LCM1602_IIC3.D0, LCD1.DB0
  N6: LCM1602_IIC3.D1, LCD1.DB1
  N7: LCM1602_IIC3.D2, LCD1.DB2
  N8: LCM1602_IIC3.D3, LCD1.DB3
  N9: LCM1602_IIC3.D4, LCD1.DB4
  N10: LCM1602_IIC3.D5, LCD1.DB5
  N11: LCM1602_IIC3.D6, LCD1.DB6
  N12: LCM1602_IIC3.D7, LCD1.DB7
  N13: LCM1602_IIC3.A, LCD1.LED+
  N14: LCM1602_IIC3.K, LCD1.LED-
  GND: LCM1602_IIC3.GND, U1.GND, DHT1.GND
  VCC: LCM1602_IIC3.VCC, U1.3.3, DHT1.VDD
  N15: LCM1602_IIC3.SDA, U1.GPIO21
  N16: LCM1602_IIC3.SCL, U1.GPIO22
  N17: LCM1602_IIC3.LED_A, LCM1602_IIC3.LED_B
  N18: U1.GPIO17, DHT1.DATA

custom parts:
  LCM1602 IIC: I2C-Module to use a 1602 or 2004 LCD on with the wire.h libory Serial LCD Modul
  ESP32S-HiLetgo: HiLetgo ESP-WROOM-32 ESP32 ESP-32S Development Board 2.4GHz Dual-Mode WiFi + Bluetooth Dual Cores Microcontroller The ESP32 integrated with Antenna switches, RF Balun, power amplifiers, low-noise amplifiers, filters, and management modules, and the entire solution occupies the least area of PCB. 2.4 GHz Wi-Fi plus Bluetooth dual-mode chip, with TSMC Ultra-low power consumption 40nm technology,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
  DHT11 Humitidy and Temperature Sensor: DHT11 Humidity and Temperature Sensor
