# Fritzing sketch ESP32_Lumex_Weather01 (saved by Fritzing 0.9.2b)
breadboards: 1

parts:
  U1 = ESP32S-HiLetgo [part_number=ESP32S-HiLetgo]
  LED1 = LED - 5mm [color="Blue (430nm)" package="5 mm [THT]"]
  +-_Tx_Rx1 = Camdenboss CTB0158-4 [part_number=CTB0158-4 package=THT]

nets:
  N1: U1.GND, LED1.cathode, +-_Tx_Rx1.pin2
  N2: U1.GPIO16, +-_Tx_Rx1.pin3
  N3: U1.GPIO17, +-_Tx_Rx1.pin4

custom parts:
  ESP32S-HiLetgo: HiLetgo ESP-WROOM-32 ESP32 ESP-32S Development Board 2.4GHz Dual-Mode WiFi + Bluetooth Dual Cores Microcontroller The ESP32 integrated with Antenna switches, RF Balun, power amplifiers, low-noise amplifiers, filters, and management modules, and the entire solution occupies the least area of PCB. 2.4 GHz Wi-Fi plus Bluetooth dual-mode chip, with TSMC Ultra-low power consumption 40nm technology,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
  Camdenboss CTB0158-4: Camdenboss CTB0158-4 5.08mm (0.2") Pitch Standard Profile 90 ̊ Rising Clamp Terminal, 4 pole The real-life connectors are modular, made up of two or three connector blocks slotted together. These can be further slotted together to make larger connectors. Fritzing part is derived from Screw terminals by Lionel Michel. Because of the offset between connection pins and screw terminals, these are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
