# Fritzing sketch ESP32_Relay (saved by Fritzing 0.9.2b)
breadboards: 1

parts:
  U1 = ESP32S-HiLetgo [part_number=ESP32S-HiLetgo]
  YwRobot_Power_Supply1 = YwRobot Breadboard Power Supply [part_number=545043]
  Part1 = KY-019 5V Relay Module [package="Breakout board"]

nets:
  N1: U1.GND, YwRobot_Power_Supply1.GND#13
  N2: U1.GPIO11, Part1.S
  N3: YwRobot_Power_Supply1.VCC#5, Part1.+
  N4: YwRobot_Power_Supply1.GND#11, Part1.-

custom parts:
  ESP32S-HiLetgo: HiLetgo ESP-WROOM-32 ESP32 ESP-32S Development Board 2.4GHz Dual-Mode WiFi + Bluetooth Dual Cores Microcontroller The ESP32 integrated with Antenna switches, RF Balun, power amplifiers, low-noise amplifiers, filters, and management modules, and the entire solution occupies the least area of PCB. 2.4 GHz Wi-Fi plus Bluetooth dual-mode chip, with TSMC Ultra-low power consumption 40nm technology,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
  YwRobot Breadboard Power Supply: The YwRobot Breadboard Power Supply (MB-V2) has two power rails; they can be 5V or 3V3. Power to the module can be provided through the female USB socket or through the A10 (female) 2.1mm power jack.
  KY-019 5V Relay Module: KY-019 5V Relay module, used to control AC circuits.
