# Fritzing sketch esp32-hmc5883l (saved by Fritzing 0.9.2b)
breadboards: 1

parts:
  Module1 = Boladge HMC5883L Compass Module
  U1 = ESP32S-HiLetgo [part_number=ESP32S-HiLetgo]

nets:
  N1: Module1.VCC, U1.3.3
  GND: Module1.GND, U1.GND
  N2: Module1.SCL, U1.GPIO22
  N3: Module1.SDA, U1.GPIO21

notes:
  GY-271 HMC5883L
  ESP-32S

custom parts:
  Boladge HMC5883L Compass Module: Cheap digital compass module
  ESP32S-HiLetgo: HiLetgo ESP-WROOM-32 ESP32 ESP-32S Development Board 2.4GHz Dual-Mode WiFi + Bluetooth Dual Cores Microcontroller The ESP32 integrated with Antenna switches, RF Balun, power amplifiers, low-noise amplifiers, filters, and management modules, and the entire solution occupies the least area of PCB. 2.4 GHz Wi-Fi plus Bluetooth dual-mode chip, with TSMC Ultra-low power consumption 40nm technology,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
