# Fritzing sketch Lolin32空版_ThreeLeds (saved by Fritzing 0.9.2b)
breadboards: 1

parts:
  U1 = lolin
  LED1 = LED - 5mm [color="Red (633nm)" package="5 mm [THT]"]
  LED2 = LED - 5mm [color="Green (570nm)" package="5 mm [THT]"]
  LED3 = LED - 5mm [color="Blue (525nm)" package="5 mm [THT]"]

nets:
  N1: U1.connector8, LED1.anode
  N2: U1.connector9, LED2.anode
  N3: U1.connector10, LED3.anode
  N4: U1.connector14, U1.connector37
  N5: LED1.cathode, LED2.cathode, LED3.cathode
