# Fritzing sketch LolinMP3 (saved by Fritzing 0.9.2b)
breadboards: 1

parts:
  U1 = lolin
  DFPlayer_Mini1 = DFPlayer MINI [package="DIP (Dual Inline) [THT]"]
  SP1 = SPEAKER [package=pcb_mount_speaker]
  SP2 = SPEAKER [package=pcb_mount_speaker]

nets:
  N1: U1.connector14, U1.connector37, DFPlayer_Mini1.VCC
  N2: U1.connector24, DFPlayer_Mini1.RX
  N3: U1.connector25, DFPlayer_Mini1.TX
  N4: DFPlayer_Mini1.GND#6, SP1.+, SP2.+
  N5: DFPlayer_Mini1.IO_1, SP1.-
  N6: DFPlayer_Mini1.IO_2, SP2.-

custom parts:
  DFPlayer MINI: MP3 module by DFRobot.com for playing Music from an SD-Card. Supports WAV and MP3 files.
