# Fritzing sketch Lolin_Light_Sword (saved by Fritzing 0.9.2b)
breadboards: 1

parts:
  U1 = lolin
  U2 = WS2812 RGB LED strip
  DFPlayer_Mini2 = DFPlayer MINI [package="DIP (Dual Inline) [THT]"]
  SP3 = SPEAKER [package=pcb_mount_speaker]
  SP4 = SPEAKER [package=pcb_mount_speaker]
  YwRobot_Power_Supply1 = YwRobot Breadboard Power Supply [part_number=545043]  # not connected

nets:
  N1: U1.connector14, DFPlayer_Mini2.VCC, SP4.+
  N2: U1.connector18, U2.DIN
  N3: U1.connector23, DFPlayer_Mini2.RX
  N4: U1.connector24, DFPlayer_Mini2.TX
  N5: U1.connector37, U2.VCC
  N6: DFPlayer_Mini2.SPK1, SP4.-
  N7: DFPlayer_Mini2.GND#6, SP3.+
  N8: DFPlayer_Mini2.SPK2, SP3.-

custom parts:
  WS2812 RGB LED strip: WS2812 strip
  DFPlayer MINI: MP3 module by DFRobot.com for playing Music from an SD-Card. Supports WAV and MP3 files.
  YwRobot Breadboard Power Supply: The YwRobot Breadboard Power Supply (MB-V2) has two power rails; they can be 5V or 3V3. Power to the module can be provided through the female USB socket or through the A10 (female) 2.1mm power jack.
