# Fritzing sketch Lolin_Light_Sword_V2 (saved by Fritzing 0.9.2b)
breadboards: 2

parts:
  YwRobot_Power_Supply2 = YwRobot Breadboard Power Supply [part_number=545043]
  DFPlayer_Mini3 = DFPlayer MINI [package="DIP (Dual Inline) [THT]"]
  U3 = lolin
  U4 = WS2812 RGB LED strip
  SP5 = SPEAKER [package=pcb_mount_speaker]
  SP6 = SPEAKER [package=pcb_mount_speaker]
  YwRobot_Power_Supply3 = YwRobot Breadboard Power Supply [part_number=545043]
  MPU-1 = Adafruit MPU6050  # not connected
  Part1 = Adafruit ADXL345 [part_number="Adafruit #1231"]  # not connected

nets:
  N1: YwRobot_Power_Supply2.VCC#5, YwRobot_Power_Supply2.VCC#6, U3.connector37
  VCC: YwRobot_Power_Supply2.VCC#9, YwRobot_Power_Supply2.VCC#10, DFPlayer_Mini3.VCC, U4.VCC
  N2: YwRobot_Power_Supply2.GND#11, YwRobot_Power_Supply2.GND#12, DFPlayer_Mini3.GND#9, U4.GND, YwRobot_Power_Supply3.GND#13, YwRobot_Power_Supply3.GND#14
  N3: YwRobot_Power_Supply2.GND#13, YwRobot_Power_Supply2.GND#14
  N4: DFPlayer_Mini3.RX, U3.connector23
  N5: DFPlayer_Mini3.TX, U3.connector24
  N6: DFPlayer_Mini3.SPK1, SP6.-
  N7: DFPlayer_Mini3.GND#6, SP5.+, SP6.+
  N8: DFPlayer_Mini3.SPK2, SP5.-
  N9: U3.connector18, U4.DIN
  N10: YwRobot_Power_Supply3.VCC#5, YwRobot_Power_Supply3.VCC#6
  N11: YwRobot_Power_Supply3.VCC#9, YwRobot_Power_Supply3.VCC#10
  N12: YwRobot_Power_Supply3.GND#11, YwRobot_Power_Supply3.GND#12

custom parts:
  YwRobot Breadboard Power Supply: The YwRobot Breadboard Power Supply (MB-V2) has two power rails; they can be 5V or 3V3. Power to the module can be provided through the female USB socket or through the A10 (female) 2.1mm power jack.
  DFPlayer MINI: MP3 module by DFRobot.com for playing Music from an SD-Card. Supports WAV and MP3 files.
  WS2812 RGB LED strip: WS2812 strip
  Adafruit MPU6050: The MPU-6050 is a popular six axis accelerometer and gyroscope (gyro) that has all the info you need on how things are shakin' and spinnin' . With six axes of sensing and 16-bit measurements, you'll have everything you need to give your robot friend an inner ear. This combination of gyroscopes and accelerometers is commonly referred to as an Inertial Measurement Unit or IMU. Not so long ago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
  Adafruit ADXL345: Filling out our accelerometer offerings, we now have the really lovely digital ADXL345 from Analog Devices, a triple-axis accelerometer with digital I2C and SPI interface breakout. We added an on-board 3.3V regulator and logic-level shifting circuitry, making it a perfect choice for interfacing with any 3V or 5V microcontroller such as the Arduino. The sensor has three axes of measurements, X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
