# Fritzing sketch Lolin_WS2812B (saved by Fritzing 0.9.2b)
breadboards: 1

parts:
  U1 = lolin
  U2 = WS2812 RGB LED strip

nets:
  N1: U1.connector14, U1.connector37, U2.VCC
  N2: U1.connector18, U2.DIN

custom parts:
  WS2812 RGB LED strip: WS2812 strip
