# Fritzing sketch NANO_基本電路_DS3231_RTC (saved by Fritzing 0.9.2b)
breadboards: 1

parts:
  Part1 = Arduino Nano (Rev3.0)
  LED1 = LED - 5mm [color="Orange (620nm)" package="5 mm [THT]"]
  R1 = Resistor [tolerance=±5% resistance=220 package=THT]
  LED2 = LED - 5mm [color="Green (570nm)" package="5 mm [THT]"]
  ZS-042_RTC1 = ZS-042 RTC Module

nets:
  GND: Part1.GND, LED2.cathode, ZS-042_RTC1.GND
  5V: Part1.5V, LED1.cathode, R1.Pin_0, ZS-042_RTC1.VCC
  N1: Part1.A5, ZS-042_RTC1.SCL
  N2: Part1.A4, ZS-042_RTC1.SDA
  N3: Part1.D13/SCK, LED1.anode
  N4: R1.Pin_1, LED2.anode
