# Fritzing sketch NANO_基本電路_LCD2004 (saved by Fritzing 0.9.2b)
breadboards: 1

parts:
  Part1 = Arduino Nano (Rev3.0)
  LED1 = LED - 5mm [color="Orange (620nm)" package="5 mm [THT]"]
  R1 = Resistor [tolerance=±5% resistance=220 package=THT]
  LED2 = LED - 5mm [color="Green (570nm)" package="5 mm [THT]"]
  LCD2004-I2C1 = LCD2004-I2C

nets:
  GND: Part1.GND, LED2.cathode, LCD2004-I2C1.GND
  5V: Part1.5V, LED1.cathode, R1.Pin_0, LCD2004-I2C1.VCC
  N1: Part1.A5, LCD2004-I2C1.SCL
  N2: Part1.A4, LCD2004-I2C1.SDA
  N3: Part1.D13/SCK, LED1.anode
  N4: R1.Pin_1, LED2.anode

custom parts:
  LCD2004-I2C: A standard character display with 4x20 characters. Comes in many colors with LCM2004 IIC attached.
