# Fritzing sketch NANO_基本電路_電源燈 (saved by Fritzing 0.9.2b)
breadboards: 1

parts:
  Part1 = Arduino Nano (Rev3.0)
  LED1 = LED - 5mm [color="Orange (620nm)" package="5 mm [THT]"]
  R1 = Resistor [tolerance=±5% resistance=220 package=THT]
  LED2 = LED - 5mm [color="Green (570nm)" package="5 mm [THT]"]

nets:
  N1: Part1.GND, LED2.cathode
  N2: Part1.5V, LED1.cathode, R1.Pin_0
  N3: Part1.D13/SCK, LED1.anode
  N4: R1.Pin_1, LED2.anode
