# Fritzing sketch WEMOS_MQx (saved by Fritzing 0.9.2b)
breadboards: 1

parts:
  WeMos_D1_R1 = WeMos D1 R2
  Part1 = MQ-4

nets:
  N1: WeMos_D1_R1.A0, Part1.AO
  N2: WeMos_D1_R1.GND#20, Part1.GND
  5V: WeMos_D1_R1.5V, Part1.VCC

custom parts:
  WeMos D1 R2: The D1 R2 is a mini wifi board based on the ESP-8266EX.
