# Fritzing sketch WeMOS_D1_R1_DHT11_OK (saved by Fritzing 0.9.2b)
breadboards: 1

parts:
  WeMos_D1_R1 = WeMos D1 R2
  Part1 = KY-015 Temperature & Humidity Sensor Module [package="Breakout board"]

nets:
  N1: WeMos_D1_R1.D8, Part1.S
  N2: WeMos_D1_R1.GND, Part1.-
  5V: WeMos_D1_R1.5V, Part1.Vin

custom parts:
  WeMos D1 R2: The D1 R2 is a mini wifi board based on the ESP-8266EX.
  KY-015 Temperature & Humidity Sensor Module: KY-015 temperature and humidity sensor module, provides a low-latency serial interface to measure humidity and temperature.
