# Fritzing sketch WeMOS_D1_R1_LCD (saved by Fritzing 0.9.2b)
breadboards: 1

parts:
  WeMos_D1_R1 = WeMos D1 R2
  LCD2004-I2C1 = LCD2004-I2C

nets:
  N1: WeMos_D1_R1.D14, LCD2004-I2C1.SDA
  N2: WeMos_D1_R1.D15, LCD2004-I2C1.SCL
  GND: WeMos_D1_R1.GND, LCD2004-I2C1.GND
  5V: WeMos_D1_R1.5V, LCD2004-I2C1.VCC

custom parts:
  WeMos D1 R2: The D1 R2 is a mini wifi board based on the ESP-8266EX.
  LCD2004-I2C: A standard character display with 4x20 characters. Comes in many colors with LCM2004 IIC attached.
