# Fritzing sketch WeMOS_D1_R1_PIR_HC-SR04 (saved by Fritzing 0.9.2b)
breadboards: 1

parts:
  WeMos_D1_R1 = WeMos D1 R2
  Part1 = HC-SR501 Body Sensor Module
  Part2 = SRF05 Ultrasonic Rangefinder

nets:
  N1: WeMos_D1_R1.(D6), Part2.Trig
  N2: WeMos_D1_R1.(D7), Part2.Echo
  N3: WeMos_D1_R1.D12, Part1.OUT
  GND: WeMos_D1_R1.GND, Part1.GND, Part2.GND
  VCC: WeMos_D1_R1.5V, Part1.VCC, Part2.VCC

custom parts:
  WeMos D1 R2: The D1 R2 is a mini wifi board based on the ESP-8266EX.
  HC-SR501 Body Sensor Module: Pyroelectric Infrared PIR Motion Sensor Detector Module
