# Fritzing sketch WeMOS_D1_R1_Relay_OK (saved by Fritzing 0.9.2b)
breadboards: 1

parts:
  WeMos_D1_R1 = WeMos D1 R2
  Part2 = KY-019 5V Relay Module [package="Breakout board"]
  LED1 = LED - 5mm [color="Red (633nm)" package="5 mm [THT]"]

nets:
  N1: WeMos_D1_R1.D8, LED1.anode
  N2: WeMos_D1_R1.D13, Part2.S
  N3: WeMos_D1_R1.GND, Part2.-, LED1.cathode
  N4: WeMos_D1_R1.5V, Part2.+

custom parts:
  WeMos D1 R2: The D1 R2 is a mini wifi board based on the ESP-8266EX.
  KY-019 5V Relay Module: KY-019 5V Relay module, used to control AC circuits.
